// Logisim project KeyboardInputAWSD.circ as structural Verilog: 1 circuit, main circuit main
module main (
);

  wire CLK_out, comparator_1_eq, comparator_2_eq, comparator_3_eq, comparator_4_eq, or_1_out;
  wire [6:0] keyboard_1_data;

  Keyboard keyboard_1 (.clk(CLK_out), .clr(or_1_out), .data(keyboard_1_data));  // open: re, avail
  Clock CLK (.out(CLK_out));
  or or_1 (or_1_out, comparator_1_eq, comparator_2_eq, comparator_3_eq, comparator_4_eq);
  DotMatrix #(.matrixcols(1), .matrixrows(1), .persist(2048)) dotmatrix_1 (.col0(comparator_1_eq));
  Comparator #(.width(7)) comparator_1 (.a(7'b1110111), .b(keyboard_1_data), .eq(comparator_1_eq));  // open: gt, lt
  DotMatrix #(.matrixcols(1), .matrixrows(1), .persist(2048)) dotmatrix_2 (.col0(comparator_2_eq));
  Comparator #(.width(7)) comparator_2 (.a(7'b1110011), .b(keyboard_1_data), .eq(comparator_2_eq));  // open: gt, lt
  DotMatrix #(.matrixcols(1), .matrixrows(1), .persist(2048)) dotmatrix_3 (.col0(comparator_3_eq));
  Comparator #(.width(7)) comparator_3 (.a(7'b1100001), .b(keyboard_1_data), .eq(comparator_3_eq));  // open: gt, lt
  DotMatrix #(.matrixcols(1), .matrixrows(1), .persist(2048)) dotmatrix_4 (.col0(comparator_4_eq));
  Comparator #(.width(7)) comparator_4 (.a(7'b1100100), .b(keyboard_1_data), .eq(comparator_4_eq));  // open: gt, lt

  // Notes on the sheet:
  //   Up (W)
  //   Down (S)
  //   Left (A)
  //   Right (D)
  //   Tak, to dziala.
  //   Up pressed
  //   Down pressed
  //   Left pressed
  //   Right pressed
endmodule
