// Logisim project SRlatch.circ as structural Verilog: 1 circuit, main circuit main
module main (
  input  RESTET,
  input  SET,
  output Q
);

  wire nor_2_out;

  nor nor_1 (Q, RESTET, nor_2_out);
  nor nor_2 (nor_2_out, Q, SET);
endmodule
