// Logisim project TEST2.circ as structural Verilog: 1 circuit, main circuit main
module main (
  input  [3:0] in_1,
  input  [3:0] in_2,
  input  in_3,
  input  [3:0] in_4,
  input  [3:0] in_5,
  input  in_6,
  input  in_7,
  input  in_8
);

  wire and_1_out, button_1_out, button_2_out, CLK, comparator_1_eq, comparator_1_lt, counter_1_carry,
       counter_2_carry, CURR_SEG_ALIVE, NEXT_SHIP, ROTATED, SHIP_DRAW_ENABLE;
  wire [1:0] SEGMENT_SEL, SHIP_TYPE;
  wire [2:0] SHIP_DRAW_SEL;
  wire [3:0] ALIVE, SHIP_X, SHIP_Y;
  wire [4:0] BL_SEL, BR_SEL, TL_SEL, TR_SEL;
  wire [5:0] main_3_out_x_00, main_3_out_x_01, main_3_out_x_10, main_3_out_x_11, main_3_out_y_00,
       main_3_out_y_01, main_3_out_y_10, main_3_out_y_11, SHIP_SCR_X, SHIP_SCR_Y;
  wire [29:0] BL_DATA, BR_DATA, demultiplexer_1_out0, demultiplexer_1_out1, demultiplexer_1_out2,
       demultiplexer_1_out3, demultiplexer_1_out4, demultiplexer_1_out5, demultiplexer_1_out6,
       demultiplexer_1_out7, demultiplexer_1_out8, demultiplexer_1_out9, demultiplexer_1_out10,
       demultiplexer_1_out11, demultiplexer_1_out12, demultiplexer_1_out13, demultiplexer_1_out14,
       demultiplexer_1_out15, demultiplexer_1_out16, demultiplexer_1_out17, demultiplexer_1_out18,
       demultiplexer_1_out19, demultiplexer_1_out20, demultiplexer_1_out21, demultiplexer_1_out22,
       demultiplexer_1_out23, demultiplexer_1_out24, demultiplexer_1_out25, demultiplexer_1_out26,
       demultiplexer_1_out27, demultiplexer_1_out28, demultiplexer_1_out29, demultiplexer_2_out0,
       demultiplexer_2_out1, demultiplexer_2_out2, demultiplexer_2_out3, demultiplexer_2_out4,
       demultiplexer_2_out5, demultiplexer_2_out6, demultiplexer_2_out7, demultiplexer_2_out8,
       demultiplexer_2_out9, demultiplexer_2_out10, demultiplexer_2_out11, demultiplexer_2_out12,
       demultiplexer_2_out13, demultiplexer_2_out14, demultiplexer_2_out15, demultiplexer_2_out16,
       demultiplexer_2_out17, demultiplexer_2_out18, demultiplexer_2_out19, demultiplexer_2_out20,
       demultiplexer_2_out21, demultiplexer_2_out22, demultiplexer_2_out23, demultiplexer_2_out24,
       demultiplexer_2_out25, demultiplexer_2_out26, demultiplexer_2_out27, demultiplexer_2_out28,
       demultiplexer_2_out29, demultiplexer_3_out0, demultiplexer_3_out1, demultiplexer_3_out2,
       demultiplexer_3_out3, demultiplexer_3_out4, demultiplexer_3_out5, demultiplexer_3_out6,
       demultiplexer_3_out7, demultiplexer_3_out8, demultiplexer_3_out9, demultiplexer_3_out10,
       demultiplexer_3_out11, demultiplexer_3_out12, demultiplexer_3_out13, demultiplexer_3_out14,
       demultiplexer_3_out15, demultiplexer_3_out16, demultiplexer_3_out17, demultiplexer_3_out18,
       demultiplexer_3_out19, demultiplexer_3_out20, demultiplexer_3_out21, demultiplexer_3_out22,
       demultiplexer_3_out23, demultiplexer_3_out24, demultiplexer_3_out25, demultiplexer_3_out26,
       demultiplexer_3_out27, demultiplexer_3_out28, demultiplexer_3_out29, demultiplexer_4_out0,
       demultiplexer_4_out1, demultiplexer_4_out2, demultiplexer_4_out3, demultiplexer_4_out4,
       demultiplexer_4_out5, demultiplexer_4_out6, demultiplexer_4_out7, demultiplexer_4_out8,
       demultiplexer_4_out9, demultiplexer_4_out10, demultiplexer_4_out11, demultiplexer_4_out12,
       demultiplexer_4_out13, demultiplexer_4_out14, demultiplexer_4_out15, demultiplexer_4_out16,
       demultiplexer_4_out17, demultiplexer_4_out18, demultiplexer_4_out19, demultiplexer_4_out20,
       demultiplexer_4_out21, demultiplexer_4_out22, demultiplexer_4_out23, demultiplexer_4_out24,
       demultiplexer_4_out25, demultiplexer_4_out26, demultiplexer_4_out27, demultiplexer_4_out28,
       demultiplexer_4_out29, TL_DATA, TR_DATA;

  Clock clock_1 (.out(CLK));
  Button button_1 (.out(button_1_out));
  Button button_2 (.out(button_2_out));
  memory_management_main main_1 (
    .X(in_1), .Y(in_2), .ROTATED(in_3), .RAM_OUT({ALIVE, ROTATED, SHIP_TYPE, SHIP_Y, SHIP_X}),
    .CHECK_X(in_4), .CHECK_Y(in_5), .SINK_IF_HIT(in_6), .CONFIRM(button_1_out), .CHECK(button_2_out),
    .CLK(CLK), .SHOW_NEXT_SHIP(NEXT_SHIP));  // open: WIN, HIT, CHECKING, CURR_SHIP_ADD, in_2
  Multiplexer #(.select(2), .enable("false")) multiplexer_1 (
    .in0(ALIVE[0]), .in1(ALIVE[1]), .in2(ALIVE[2]), .in3(ALIVE[3]), .out(CURR_SEG_ALIVE), .sel(SEGMENT_SEL));
  Multiplexer #(.width(3), .enable("false")) multiplexer_2 (
    .in0(3'b010), .in1(3'b001), .out(SHIP_DRAW_SEL), .sel(CURR_SEG_ALIVE));
  Comparator #(.width(2), .mode("unsigned")) comparator_1 (
    .a(SEGMENT_SEL), .b(SHIP_TYPE), .eq(comparator_1_eq), .lt(comparator_1_lt));  // open: gt
  or or_1 (SHIP_DRAW_ENABLE, comparator_1_eq, comparator_1_lt);
  Counter #(.width(3), .max('h4)) counter_1 (.carry(counter_1_carry), .clk(CLK));  // open: load, D, count, Q, clr
  Counter #(.width(2), .max('h3)) counter_2 (
    .Q(SEGMENT_SEL), .carry(counter_2_carry), .clk(counter_1_carry));  // open: load, D, count, clr
  and and_1 (and_1_out, counter_2_carry, in_7);
  or or_2 (NEXT_SHIP, and_1_out, in_8);
  screen_xy_to_screen_data_main main_2 (
    .SCREEN_X(SHIP_SCR_X), .SCREEN_Y(SHIP_SCR_Y), .DATA_TO_DISPLAY(SHIP_DRAW_SEL), .TL_SEL_OUT(TL_SEL),
    .TR_SEL_OUT(TR_SEL), .BL_SEL_OUT(BL_SEL), .BR_SEL_OUT(BR_SEL), .TL_DATA_OUT(TL_DATA),
    .TR_DATA_OUT(TR_DATA), .BL_DATA_OUT(BL_DATA), .BR_DATA_OUT(BR_DATA), .CLK(CLK), .ENABLE(SHIP_DRAW_ENABLE));
  ship_xyr_to_screen_xy_main main_3 (
    .in_1(SHIP_X), .in_2(SHIP_Y), .in_3(ROTATED), .OUT_X_00(main_3_out_x_00), .OUT_Y_00(main_3_out_y_00),
    .OUT_X_01(main_3_out_x_01), .OUT_Y_01(main_3_out_y_01), .OUT_X_10(main_3_out_x_10),
    .OUT_Y_10(main_3_out_y_10), .OUT_X_11(main_3_out_x_11), .OUT_Y_11(main_3_out_y_11));
  Multiplexer #(.select(2), .width(6), .enable("false")) multiplexer_3 (
    .in0(main_3_out_x_00), .in1(main_3_out_x_01), .in2(main_3_out_x_10), .in3(main_3_out_x_11),
    .out(SHIP_SCR_X), .sel(SEGMENT_SEL));
  Multiplexer #(.select(2), .width(6), .enable("false")) multiplexer_4 (
    .in0(main_3_out_y_00), .in1(main_3_out_y_01), .in2(main_3_out_y_10), .in3(main_3_out_y_11),
    .out(SHIP_SCR_Y), .sel(SEGMENT_SEL));
  DotMatrix #(.matrixcols(30), .matrixrows(30), .persist(500)) dotmatrix_1 (
    .col0(demultiplexer_1_out0), .col1(demultiplexer_1_out1), .col2(demultiplexer_1_out2),
    .col3(demultiplexer_1_out3), .col4(demultiplexer_1_out4), .col5(demultiplexer_1_out5),
    .col6(demultiplexer_1_out6), .col7(demultiplexer_1_out7), .col8(demultiplexer_1_out8),
    .col9(demultiplexer_1_out9), .col10(demultiplexer_1_out10), .col11(demultiplexer_1_out11),
    .col12(demultiplexer_1_out12), .col13(demultiplexer_1_out13), .col14(demultiplexer_1_out14),
    .col15(demultiplexer_1_out15), .col16(demultiplexer_1_out16), .col17(demultiplexer_1_out17),
    .col18(demultiplexer_1_out18), .col19(demultiplexer_1_out19), .col20(demultiplexer_1_out20),
    .col21(demultiplexer_1_out21), .col22(demultiplexer_1_out22), .col23(demultiplexer_1_out23),
    .col24(demultiplexer_1_out24), .col25(demultiplexer_1_out25), .col26(demultiplexer_1_out26),
    .col27(demultiplexer_1_out27), .col28(demultiplexer_1_out28), .col29(demultiplexer_1_out29));
  DotMatrix #(.matrixcols(30), .matrixrows(30), .persist(500)) dotmatrix_2 (
    .col0(demultiplexer_2_out0), .col1(demultiplexer_2_out1), .col2(demultiplexer_2_out2),
    .col3(demultiplexer_2_out3), .col4(demultiplexer_2_out4), .col5(demultiplexer_2_out5),
    .col6(demultiplexer_2_out6), .col7(demultiplexer_2_out7), .col8(demultiplexer_2_out8),
    .col9(demultiplexer_2_out9), .col10(demultiplexer_2_out10), .col11(demultiplexer_2_out11),
    .col12(demultiplexer_2_out12), .col13(demultiplexer_2_out13), .col14(demultiplexer_2_out14),
    .col15(demultiplexer_2_out15), .col16(demultiplexer_2_out16), .col17(demultiplexer_2_out17),
    .col18(demultiplexer_2_out18), .col19(demultiplexer_2_out19), .col20(demultiplexer_2_out20),
    .col21(demultiplexer_2_out21), .col22(demultiplexer_2_out22), .col23(demultiplexer_2_out23),
    .col24(demultiplexer_2_out24), .col25(demultiplexer_2_out25), .col26(demultiplexer_2_out26),
    .col27(demultiplexer_2_out27), .col28(demultiplexer_2_out28), .col29(demultiplexer_2_out29));
  Demultiplexer #(.select(5), .width(30), .enable("false")) demultiplexer_1 (
    .out0(demultiplexer_1_out0), .out1(demultiplexer_1_out1), .out2(demultiplexer_1_out2),
    .out3(demultiplexer_1_out3), .out4(demultiplexer_1_out4), .out5(demultiplexer_1_out5),
    .out6(demultiplexer_1_out6), .out7(demultiplexer_1_out7), .out8(demultiplexer_1_out8),
    .out9(demultiplexer_1_out9), .out10(demultiplexer_1_out10), .out11(demultiplexer_1_out11),
    .out12(demultiplexer_1_out12), .out13(demultiplexer_1_out13), .out14(demultiplexer_1_out14),
    .out15(demultiplexer_1_out15), .out16(demultiplexer_1_out16), .out17(demultiplexer_1_out17),
    .out18(demultiplexer_1_out18), .out19(demultiplexer_1_out19), .out20(demultiplexer_1_out20),
    .out21(demultiplexer_1_out21), .out22(demultiplexer_1_out22), .out23(demultiplexer_1_out23),
    .out24(demultiplexer_1_out24), .out25(demultiplexer_1_out25), .out26(demultiplexer_1_out26),
    .out27(demultiplexer_1_out27), .out28(demultiplexer_1_out28), .out29(demultiplexer_1_out29),
    .in(TL_DATA), .sel(TL_SEL));  // open: out30, out31
  Demultiplexer #(.select(5), .width(30), .enable("false")) demultiplexer_2 (
    .out0(demultiplexer_2_out0), .out1(demultiplexer_2_out1), .out2(demultiplexer_2_out2),
    .out3(demultiplexer_2_out3), .out4(demultiplexer_2_out4), .out5(demultiplexer_2_out5),
    .out6(demultiplexer_2_out6), .out7(demultiplexer_2_out7), .out8(demultiplexer_2_out8),
    .out9(demultiplexer_2_out9), .out10(demultiplexer_2_out10), .out11(demultiplexer_2_out11),
    .out12(demultiplexer_2_out12), .out13(demultiplexer_2_out13), .out14(demultiplexer_2_out14),
    .out15(demultiplexer_2_out15), .out16(demultiplexer_2_out16), .out17(demultiplexer_2_out17),
    .out18(demultiplexer_2_out18), .out19(demultiplexer_2_out19), .out20(demultiplexer_2_out20),
    .out21(demultiplexer_2_out21), .out22(demultiplexer_2_out22), .out23(demultiplexer_2_out23),
    .out24(demultiplexer_2_out24), .out25(demultiplexer_2_out25), .out26(demultiplexer_2_out26),
    .out27(demultiplexer_2_out27), .out28(demultiplexer_2_out28), .out29(demultiplexer_2_out29),
    .in(BL_DATA), .sel(BL_SEL));  // open: out30, out31
  DotMatrix #(.matrixcols(30), .matrixrows(30), .persist(500)) dotmatrix_3 (
    .col0(demultiplexer_3_out0), .col1(demultiplexer_3_out1), .col2(demultiplexer_3_out2),
    .col3(demultiplexer_3_out3), .col4(demultiplexer_3_out4), .col5(demultiplexer_3_out5),
    .col6(demultiplexer_3_out6), .col7(demultiplexer_3_out7), .col8(demultiplexer_3_out8),
    .col9(demultiplexer_3_out9), .col10(demultiplexer_3_out10), .col11(demultiplexer_3_out11),
    .col12(demultiplexer_3_out12), .col13(demultiplexer_3_out13), .col14(demultiplexer_3_out14),
    .col15(demultiplexer_3_out15), .col16(demultiplexer_3_out16), .col17(demultiplexer_3_out17),
    .col18(demultiplexer_3_out18), .col19(demultiplexer_3_out19), .col20(demultiplexer_3_out20),
    .col21(demultiplexer_3_out21), .col22(demultiplexer_3_out22), .col23(demultiplexer_3_out23),
    .col24(demultiplexer_3_out24), .col25(demultiplexer_3_out25), .col26(demultiplexer_3_out26),
    .col27(demultiplexer_3_out27), .col28(demultiplexer_3_out28), .col29(demultiplexer_3_out29));
  DotMatrix #(.matrixcols(30), .matrixrows(30), .persist(500)) dotmatrix_4 (
    .col0(demultiplexer_4_out0), .col1(demultiplexer_4_out1), .col2(demultiplexer_4_out2),
    .col3(demultiplexer_4_out3), .col4(demultiplexer_4_out4), .col5(demultiplexer_4_out5),
    .col6(demultiplexer_4_out6), .col7(demultiplexer_4_out7), .col8(demultiplexer_4_out8),
    .col9(demultiplexer_4_out9), .col10(demultiplexer_4_out10), .col11(demultiplexer_4_out11),
    .col12(demultiplexer_4_out12), .col13(demultiplexer_4_out13), .col14(demultiplexer_4_out14),
    .col15(demultiplexer_4_out15), .col16(demultiplexer_4_out16), .col17(demultiplexer_4_out17),
    .col18(demultiplexer_4_out18), .col19(demultiplexer_4_out19), .col20(demultiplexer_4_out20),
    .col21(demultiplexer_4_out21), .col22(demultiplexer_4_out22), .col23(demultiplexer_4_out23),
    .col24(demultiplexer_4_out24), .col25(demultiplexer_4_out25), .col26(demultiplexer_4_out26),
    .col27(demultiplexer_4_out27), .col28(demultiplexer_4_out28), .col29(demultiplexer_4_out29));
  Demultiplexer #(.select(5), .width(30), .enable("false")) demultiplexer_3 (
    .out0(demultiplexer_3_out0), .out1(demultiplexer_3_out1), .out2(demultiplexer_3_out2),
    .out3(demultiplexer_3_out3), .out4(demultiplexer_3_out4), .out5(demultiplexer_3_out5),
    .out6(demultiplexer_3_out6), .out7(demultiplexer_3_out7), .out8(demultiplexer_3_out8),
    .out9(demultiplexer_3_out9), .out10(demultiplexer_3_out10), .out11(demultiplexer_3_out11),
    .out12(demultiplexer_3_out12), .out13(demultiplexer_3_out13), .out14(demultiplexer_3_out14),
    .out15(demultiplexer_3_out15), .out16(demultiplexer_3_out16), .out17(demultiplexer_3_out17),
    .out18(demultiplexer_3_out18), .out19(demultiplexer_3_out19), .out20(demultiplexer_3_out20),
    .out21(demultiplexer_3_out21), .out22(demultiplexer_3_out22), .out23(demultiplexer_3_out23),
    .out24(demultiplexer_3_out24), .out25(demultiplexer_3_out25), .out26(demultiplexer_3_out26),
    .out27(demultiplexer_3_out27), .out28(demultiplexer_3_out28), .out29(demultiplexer_3_out29),
    .in(TR_DATA), .sel(TR_SEL));  // open: out30, out31
  Demultiplexer #(.select(5), .width(30), .enable("false")) demultiplexer_4 (
    .out0(demultiplexer_4_out0), .out1(demultiplexer_4_out1), .out2(demultiplexer_4_out2),
    .out3(demultiplexer_4_out3), .out4(demultiplexer_4_out4), .out5(demultiplexer_4_out5),
    .out6(demultiplexer_4_out6), .out7(demultiplexer_4_out7), .out8(demultiplexer_4_out8),
    .out9(demultiplexer_4_out9), .out10(demultiplexer_4_out10), .out11(demultiplexer_4_out11),
    .out12(demultiplexer_4_out12), .out13(demultiplexer_4_out13), .out14(demultiplexer_4_out14),
    .out15(demultiplexer_4_out15), .out16(demultiplexer_4_out16), .out17(demultiplexer_4_out17),
    .out18(demultiplexer_4_out18), .out19(demultiplexer_4_out19), .out20(demultiplexer_4_out20),
    .out21(demultiplexer_4_out21), .out22(demultiplexer_4_out22), .out23(demultiplexer_4_out23),
    .out24(demultiplexer_4_out24), .out25(demultiplexer_4_out25), .out26(demultiplexer_4_out26),
    .out27(demultiplexer_4_out27), .out28(demultiplexer_4_out28), .out29(demultiplexer_4_out29),
    .in(BR_DATA), .sel(BR_SEL));  // open: out30, out31

  // Notes on the sheet:
  //   sunk
  //   alive
  //   ten mini uklad tu do testow tylko
  //   ^ do tego mozna done dodac ze skonczyl rysowac
endmodule
