// Logisim project arrow.circ as structural Verilog: 1 circuit, main circuit main
module main (
  input  in_1
);

  wire [3:0] bit_extender_1_out;
  wire [19:0] rom_1_data, rom_2_data;

  assign bit_extender_1_out = {{3{1'b0}}, in_1};  // Bit_Extender bit_extender_1
  ROM #(.addrWidth(4), .dataWidth(20)) rom_1 (.addr(bit_extender_1_out), .data(rom_1_data));  // open: sel
  ROM #(.addrWidth(4), .dataWidth(20)) rom_2 (.addr(bit_extender_1_out), .data(rom_2_data));  // open: sel
  DotMatrix #(.matrixcols(8), .matrixrows(5)) dotmatrix_1 (
    .col0(rom_1_data[19:15]), .col1(rom_1_data[14:10]), .col2(rom_1_data[9:5]), .col3(rom_1_data[4:0]),
    .col4(rom_2_data[19:15]), .col5(rom_2_data[14:10]), .col6(rom_2_data[9:5]), .col7(rom_2_data[4:0]));

  // Notes on the sheet:
  //   contents of rom_1 (hex, n*v repeats v):
  //   11d5 1084
  //   contents of rom_2 (hex, n*v repeats v):
  //   21080 ab880
endmodule
