// Logisim project bots.circ as structural Verilog: 1 circuit, main circuit main
module main (
  input  CURR_PLAYER,
  input  PREP_PHASE_END,
  input  CHECKING,
  input  CLR,
  input  WIN,
  input  CLK,
  input  HIT,
  input  [3:0] SHIPS_NUMBER,
  output ROTATED,
  output CONFIRM,
  output [3:0] X,
  output [3:0] Y
);

  wire _1ST_SHOT_DONE, _10SHIPS, and_2_out, and_4_out, BOOT_PHASE, comparator_1_eq, comparator_1_gt,
       controlled_buffer_1_out, controlled_buffer_5_out, counter_1_carry, counter_2_carry, d_ff_1_q,
       d_ff_2_q, d_ff_3_qn, demultiplexer_1_out0, demultiplexer_1_out1, demultiplexer_1_out2, not_1_out,
       not_3_out, not_4_out, not_5_out, or_2_out, or_3_out, POSITION_CLOCK, random_1_out, ROTATION_CLOCK,
       SHOOT, SHOOT1, SHOOT2, SHOOT_PHASE, SHOT_DONE;
  wire [4:0] counter_2_q, counter_3_q;

  Clock clock_1 ();  // open: out
  D_Flip_Flop d_ff_1 (.clk(SHOOT), .D(SHOOT), .Q(d_ff_1_q), .reset(counter_2_carry));  // open: Qn, preset, en
  Pull_Resistor pull_resistor_1 (.node(SHOOT));
  and and_1 (SHOOT_PHASE, CURR_PLAYER, PREP_PHASE_END);
  not not_1 (not_1_out, PREP_PHASE_END);
  not not_2 (not_1_out, PREP_PHASE_END);
  not not_3 (not_3_out, _10SHIPS);
  and and_2 (and_2_out, BOOT_PHASE, CLK);
  Counter #(.width(1), .max('h1)) counter_1 (
    .carry(counter_1_carry), .clk(controlled_buffer_1_out));  // open: load, D, count, Q, clr
  Counter #(.width(5), .max('h1f)) counter_2 (
    .Q(counter_2_q), .carry(counter_2_carry), .clk(counter_1_carry), .clr(counter_2_carry));  // open: load, D, count
  assign controlled_buffer_1_out = d_ff_1_q ? CLK : 1'bz;  // Controlled_Buffer controlled_buffer_1
  Pull_Resistor pull_resistor_2 (.node(controlled_buffer_1_out));
  and and_3 (BOOT_PHASE, not_1_out, not_3_out);
  Comparator #(.width(4), .mode("unsigned")) comparator_1 (
    .a(SHIPS_NUMBER), .b(4'b1010), .gt(comparator_1_gt), .eq(comparator_1_eq));  // open: lt
  Demultiplexer #(.select(5)) demultiplexer_1 (
    .out0(demultiplexer_1_out0), .out1(demultiplexer_1_out1), .out2(demultiplexer_1_out2), .in(1'b1),
    .sel(counter_3_q));  // open: out3, out4, out5, out6, out7, out8, out9, out10, out11, out12, out13, out14, out15, out16, out17, out18, out19, out20, out21, out22, out23, out24, out25, out26, out27, out28, out29, out30, out31, en
  Counter #(.width(5), .max('h1f)) counter_3 (
    .Q(counter_3_q), .clk(and_2_out), .clr(CLR));  // open: load, D, count, carry
  Demultiplexer #(.select(5)) demultiplexer_2 (
    .out2(POSITION_CLOCK), .out4(CONFIRM), .out30(SHOT_DONE), .in(1'b1), .sel(counter_2_q), .en(d_ff_1_q));  // open: out0, out1, out3, out5, out6, out7, out8, out9, out10, out11, out12, out13, out14, out15, out16, out17, out18, out19, out20, out21, out22, out23, out24, out25, out26, out27, out28, out29, out31
  or or_1 (_10SHIPS, comparator_1_gt, comparator_1_eq);
  Pull_Resistor pull_resistor_3 (.node(SHOT_DONE));
  assign ROTATION_CLOCK = and_2_out ? demultiplexer_1_out0 : 1'bz;  // Controlled_Buffer controlled_buffer_2
  assign POSITION_CLOCK = and_2_out ? demultiplexer_1_out1 : 1'bz;  // Controlled_Buffer controlled_buffer_3
  assign CONFIRM = and_2_out ? demultiplexer_1_out2 : 1'bz;  // Controlled_Buffer controlled_buffer_4
  D_Flip_Flop d_ff_2 (.clk(SHOT_DONE), .D(SHOT_DONE), .Q(d_ff_2_q), .reset(or_2_out));  // open: Qn, preset, en
  or or_2 (or_2_out, not_4_out, SHOOT2);
  not not_4 (not_4_out, SHOOT_PHASE);
  D_Flip_Flop d_ff_3 (
    .clk(SHOT_DONE), .D(SHOT_DONE), .Q(_1ST_SHOT_DONE), .Qn(d_ff_3_qn), .reset(not_5_out));  // open: preset, en
  assign controlled_buffer_5_out = d_ff_3_qn ? SHOOT_PHASE : 1'bz;  // Controlled_Buffer controlled_buffer_5
  not not_5 (not_5_out, SHOOT_PHASE);
  tick_main main_1 (.in_1(CLK), .in_2(and_4_out), .out_3(SHOOT2));
  and and_4 (and_4_out, d_ff_2_q, SHOOT_PHASE, _1ST_SHOT_DONE);
  tick_main main_2 (.in_1(CLK), .in_2(controlled_buffer_5_out), .out_3(SHOOT1));
  or or_3 (or_3_out, SHOOT1, SHOOT2);
  and and_5 (SHOOT, SHOOT_PHASE, or_3_out);
  Pull_Resistor pull_resistor_4 (.node(ROTATION_CLOCK));
  Pull_Resistor pull_resistor_5 (.node(POSITION_CLOCK));
  Random #(.width(1)) random_1 (.clk(ROTATION_CLOCK), .next(ROTATION_CLOCK), .out(random_1_out));  // open: clr
  Counter #(.width(1), .max('h1)) counter_4 (
    .Q(ROTATED), .clk(random_1_out), .clr(CLR));  // open: load, D, count, carry
  Pull_Resistor pull_resistor_6 (.node(CONFIRM));
  random_num_generator_A_main main_3 (.GENERATE(POSITION_CLOCK), .OUTPUT(X));
  random_num_generator_B_main main_4 (.GENERATE(POSITION_CLOCK), .OUTPUT(Y));

  // Other names for the same wires on the sheet: CONFIRM_CLOCK = CONFIRM; SHIP_NUMBER[3:0] = SHIPS_NUMBER
endmodule
