// Logisim project game.circ as structural Verilog: 1 circuit, main circuit main
module main (
  input  in_1,
  input  in_2
);

  wire K1CLK, K1RST, K2CLK, K2RST, main_2_out_2, main_2_out_3, main_2_out_4, main_2_out_5, main_2_out_6,
       main_2_out_7, main_2_out_8, main_2_out_9, main_2_out_10, main_2_out_11, main_2_out_12, main_2_out_13,
       main_2_out_14, main_2_out_15, main_2_out_16, main_2_out_17, main_2_out_18, main_2_out_19,
       main_2_out_20, main_2_out_21, main_2_out_22, main_2_out_23, main_2_out_24, main_2_out_25,
       main_2_out_26, main_2_out_27, main_2_out_28, main_2_out_29, main_2_out_30, main_2_out_31,
       main_2_out_32, main_2_out_33, main_3_out_2, main_3_out_3, main_3_out_4, main_3_out_5, main_3_out_6,
       main_3_out_7, main_3_out_8, main_3_out_9, main_3_out_10, main_3_out_11, main_3_out_12, main_3_out_13,
       main_3_out_14, main_3_out_15, main_3_out_16, main_3_out_17, main_3_out_18, main_3_out_19,
       main_3_out_20, main_3_out_21, main_3_out_22, main_3_out_23, main_3_out_24, main_3_out_25,
       main_3_out_26, main_3_out_27, main_3_out_28, main_3_out_29, main_3_out_30, main_3_out_31,
       main_3_out_32, main_3_out_33, main_4_out_2, main_4_out_3, main_4_out_4, main_4_out_5, main_4_out_6,
       main_4_out_7, main_4_out_8, main_4_out_9, main_4_out_10, main_4_out_11, main_4_out_12, main_4_out_13,
       main_4_out_14, main_4_out_15, main_4_out_16, main_4_out_17, main_4_out_18, main_4_out_19,
       main_4_out_20, main_4_out_21, main_4_out_22, main_4_out_23, main_4_out_24, main_4_out_25,
       main_4_out_26, main_4_out_27, main_4_out_28, main_4_out_29, main_4_out_30, main_4_out_31,
       main_4_out_32, main_4_out_33, main_5_out_2, main_5_out_3, main_5_out_4, main_5_out_5, main_5_out_6,
       main_5_out_7, main_5_out_8, main_5_out_9, main_5_out_10, main_5_out_11, main_5_out_12, main_5_out_13,
       main_5_out_14, main_5_out_15, main_5_out_16, main_5_out_17, main_5_out_18, main_5_out_19,
       main_5_out_20, main_5_out_21, main_5_out_22, main_5_out_23, main_5_out_24, main_5_out_25,
       main_5_out_26, main_5_out_27, main_5_out_28, main_5_out_29, main_5_out_30, main_5_out_31,
       main_5_out_32, main_5_out_33;
  wire [4:0] main_1_p248, main_1_p249, main_1_p250, main_1_p251, main_1_p252, main_1_p253, main_1_p254,
       main_1_p255;
  wire [6:0] K1DATA, K2DATA;
  wire [9:0] main_1_p244, main_1_p245, main_1_p246, main_1_p247;
  wire [29:0] main_1_p1, main_1_p2, main_1_p3, main_1_p4, main_1_p5, main_1_p6, main_1_p7, main_1_p8,
       main_1_p9, main_1_p10, main_1_p11, main_1_p12, main_1_p13, main_1_p14, main_1_p15, main_1_p16,
       main_1_p17, main_1_p18, main_1_p19, main_1_p20, main_1_p21, main_1_p22, main_1_p23, main_1_p24,
       main_1_p25, main_1_p26, main_1_p27, main_1_p28, main_1_p29, main_1_p30, main_1_p31, main_1_p32,
       main_1_p33, main_1_p34, main_1_p35, main_1_p36, main_1_p37, main_1_p38, main_1_p39, main_1_p40,
       main_1_p41, main_1_p42, main_1_p43, main_1_p44, main_1_p45, main_1_p46, main_1_p47, main_1_p48,
       main_1_p49, main_1_p50, main_1_p51, main_1_p52, main_1_p53, main_1_p54, main_1_p55, main_1_p56,
       main_1_p57, main_1_p58, main_1_p59, main_1_p60, main_1_p61, main_1_p62, main_1_p63, main_1_p64,
       main_1_p65, main_1_p66, main_1_p67, main_1_p68, main_1_p69, main_1_p70, main_1_p71, main_1_p72,
       main_1_p73, main_1_p74, main_1_p75, main_1_p76, main_1_p77, main_1_p78, main_1_p79, main_1_p80,
       main_1_p81, main_1_p82, main_1_p83, main_1_p84, main_1_p85, main_1_p86, main_1_p88, main_1_p89,
       main_1_p90, main_1_p91, main_1_p92, main_1_p93, main_1_p94, main_1_p95, main_1_p97, main_1_p98,
       main_1_p99, main_1_p100, main_1_p101, main_1_p102, main_1_p103, main_1_p104, main_1_p105, main_1_p106,
       main_1_p107, main_1_p108, main_1_p109, main_1_p110, main_1_p111, main_1_p112, main_1_p113,
       main_1_p114, main_1_p115, main_1_p116, main_1_p117, main_1_p118, main_1_p119, main_1_p120,
       main_1_p121, main_1_p122, main_1_p123, main_1_p124, main_1_p125, main_1_p126, main_1_p127,
       main_1_p128, main_1_p129, main_1_p130, main_1_p131, main_1_p132, main_1_p133, main_1_p134,
       main_1_p135, main_1_p136, main_1_p137, main_1_p138, main_1_p139, main_1_p140, main_1_p141,
       main_1_p142, main_1_p143, main_1_p144, main_1_p146, main_1_p147, main_1_p148, main_1_p149,
       main_1_p150, main_1_p151, main_1_p152, main_1_p153, main_1_p154, main_1_p155, main_1_p156,
       main_1_p157, main_1_p158, main_1_p159, main_1_p160, main_1_p161, main_1_p162, main_1_p163,
       main_1_p164, main_1_p165, main_1_p166, main_1_p167, main_1_p168, main_1_p169, main_1_p170,
       main_1_p171, main_1_p172, main_1_p173, main_1_p174, main_1_p175, main_1_p176, main_1_p177,
       main_1_p178, main_1_p179, main_1_p180, main_1_p181, main_1_p182, main_1_p183, main_1_p184,
       main_1_p185, main_1_p186, main_1_p187, main_1_p188, main_1_p189, main_1_p190, main_1_p191,
       main_1_p192, main_1_p193, main_1_p194, main_1_p195, main_1_p196, main_1_p197, main_1_p198,
       main_1_p199, main_1_p200, main_1_p201, main_1_p202, main_1_p203, main_1_p204, main_1_p205,
       main_1_p206, main_1_p207, main_1_p208, main_1_p209, main_1_p210, main_1_p211, main_1_p212,
       main_1_p213, main_1_p214, main_1_p215, main_1_p216, main_1_p217, main_1_p218, main_1_p219,
       main_1_p220, main_1_p221, main_1_p222, main_1_p223, main_1_p224, main_1_p225, main_1_p226,
       main_1_p227, main_1_p228, main_1_p229, main_1_p230, main_1_p231, main_1_p232, main_1_p233,
       main_1_p234, main_1_p235, main_1_p236, main_1_p237, main_1_p238, main_1_p239, main_1_p240,
       main_1_p241, main_1_p242, main_1_p243, main_1_p256, main_1_p257, main_1_p258, main_1_p259,
       main_1_p260, main_1_p261, main_1_p262, main_1_p263, main_1_p264, main_1_p265, main_1_p266,
       main_1_p267, main_1_p268, main_1_p269, main_1_p270, main_1_p271, main_1_p272, main_1_p273,
       main_1_p274, main_1_p275, main_1_p276, main_1_p277, main_1_p278, main_1_p279, main_1_p280,
       main_1_p281, main_1_p282, main_1_p283, main_1_p284, main_1_p285, main_1_p286, main_1_p287,
       main_1_p288, main_1_p289, main_1_p290, main_1_p291, main_1_p292, main_1_p293, main_1_p294,
       main_1_p295, main_1_p296, main_1_p297, main_1_p298, main_1_p299, main_1_p300, main_1_p301,
       main_1_p302, main_1_p303, main_1_p304, main_1_p305, main_1_p306, main_1_p307, main_1_p308,
       main_1_p309, main_1_p310, main_1_p311, main_1_p312, main_1_p313, main_1_p314, main_1_p315,
       main_1_p316, main_1_p317, main_1_p318, main_1_p319, main_1_p320, main_1_p321, main_1_p322,
       main_1_p323, main_1_p324, main_1_p325, main_1_p326, main_1_p327, main_1_p328, main_1_p329,
       main_1_p330, main_1_p331, main_1_p332, main_1_p333, main_1_p334, main_1_p335, main_1_p336,
       main_1_p337, main_1_p338, main_1_p339, main_1_p340, main_1_p341, main_1_p342, main_1_p343,
       main_1_p344, main_1_p345, main_1_p346, main_1_p347, main_1_p348, main_1_p349, main_1_p350,
       main_1_p351, main_1_p352, main_1_p353, main_1_p354, main_1_p355, main_1_p356, main_1_p357,
       main_1_p358, main_1_p359, main_1_p360, main_1_p361, main_1_p363, main_1_p364, main_1_p365,
       main_1_p366, main_1_p367, main_1_p368, main_1_p369, main_1_p370, main_1_p372, main_1_p373,
       main_1_p374, main_1_p375, main_1_p376, main_1_p377, main_1_p378, main_1_p379, main_1_p380,
       main_1_p381, main_1_p382, main_1_p383, main_1_p384, main_1_p385, main_1_p386, main_1_p387,
       main_1_p388, main_1_p389, main_1_p390, main_1_p391, main_1_p392, main_1_p393, main_1_p394,
       main_1_p395, main_1_p396, main_1_p397, main_1_p398, main_1_p399, main_1_p400, main_1_p401,
       main_1_p402, main_1_p403, main_1_p404, main_1_p405, main_1_p406, main_1_p407, main_1_p408,
       main_1_p409, main_1_p410, main_1_p411, main_1_p412, main_1_p413, main_1_p414, main_1_p415,
       main_1_p416, main_1_p417, main_1_p418, main_1_p419, main_1_p421, main_1_p422, main_1_p423,
       main_1_p424, main_1_p425, main_1_p426, main_1_p427, main_1_p428, main_1_p429, main_1_p430,
       main_1_p431, main_1_p432, main_1_p433, main_1_p434, main_1_p435, main_1_p436, main_1_p437,
       main_1_p438, main_1_p439, main_1_p440, main_1_p441, main_1_p442, main_1_p443, main_1_p444,
       main_1_p445, main_1_p446, main_1_p447, main_1_p448, main_1_p449, main_1_p450, main_1_p451,
       main_1_p452, main_1_p453, main_1_p454, main_1_p455, main_1_p456, main_1_p457, main_1_p458,
       main_1_p459, main_1_p460, main_1_p461, main_1_p462, main_1_p463, main_1_p464, main_1_p465,
       main_1_p466, main_1_p467, main_1_p468, main_1_p469, main_1_p470, main_1_p471, main_1_p472,
       main_1_p473, main_1_p474, main_1_p475, main_1_p476, main_1_p477, main_1_p478, main_1_p479,
       main_1_p480, main_1_p481, main_1_p482, main_1_p483, main_1_p484, main_1_p485, main_1_p486,
       main_1_p487, main_1_p488, main_1_p489, main_1_p490, main_1_p491, main_1_p492, main_1_p493,
       main_1_p494, main_1_p495, main_1_p496, main_1_p497, main_1_p498;

  // app_main main_1: pin names not known; wires that end beside it: main_1_p1, main_1_p2, main_1_p3, main_1_p4, main_1_p5, main_1_p6, main_1_p7, main_1_p8, main_1_p9, main_1_p10, main_1_p11, main_1_p12, main_1_p13, main_1_p14, main_1_p15, main_1_p16, main_1_p17, main_1_p18, main_1_p19, main_1_p20, main_1_p21, main_1_p22, main_1_p23, main_1_p24, main_1_p25, main_1_p26, main_1_p27, main_1_p28, main_1_p29, main_1_p30, main_1_p31, main_1_p32, main_1_p33, main_1_p34, main_1_p35, main_1_p36, main_1_p37, main_1_p38, main_1_p39, main_1_p40, main_1_p41, main_1_p42, main_1_p43, main_1_p44, main_1_p45, main_1_p46, main_1_p47, main_1_p48, main_1_p49, main_1_p50, main_1_p51, main_1_p52, main_1_p53, main_1_p54, main_1_p55, main_1_p56, main_1_p57, main_1_p58, main_1_p59, main_1_p60, main_1_p61, main_1_p62, main_1_p63, main_1_p64, main_1_p65, main_1_p66, main_1_p67, main_1_p68, main_1_p69, main_1_p70, main_1_p71, main_1_p72, main_1_p73, main_1_p74, main_1_p75, main_1_p76, main_1_p77, main_1_p78, main_1_p79, main_1_p80, main_1_p81, main_1_p82, main_1_p83, main_1_p84, main_1_p85, main_1_p86, K1CLK, main_1_p88, main_1_p89, main_1_p90, main_1_p91, main_1_p92, main_1_p93, main_1_p94, main_1_p95, K1RST, main_1_p97, main_1_p98, main_1_p99, main_1_p100, main_1_p101, main_1_p102, main_1_p103, main_1_p104, main_1_p105, main_1_p106, main_1_p107, main_1_p108, main_1_p109, main_1_p110, main_1_p111, main_1_p112, main_1_p113, main_1_p114, main_1_p115, main_1_p116, main_1_p117, main_1_p118, main_1_p119, main_1_p120, main_1_p121, main_1_p122, main_1_p123, main_1_p124, main_1_p125, main_1_p126, main_1_p127, main_1_p128, main_1_p129, main_1_p130, main_1_p131, main_1_p132, main_1_p133, main_1_p134, main_1_p135, main_1_p136, main_1_p137, main_1_p138, main_1_p139, main_1_p140, main_1_p141, main_1_p142, main_1_p143, main_1_p144, K1DATA, main_1_p146, main_1_p147, main_1_p148, main_1_p149, main_1_p150, main_1_p151, main_1_p152, main_1_p153, main_1_p154, main_1_p155, main_1_p156, main_1_p157, main_1_p158, main_1_p159, main_1_p160, main_1_p161, main_1_p162, main_1_p163, main_1_p164, main_1_p165, main_1_p166, main_1_p167, main_1_p168, main_1_p169, main_1_p170, main_1_p171, main_1_p172, main_1_p173, main_1_p174, main_1_p175, main_1_p176, main_1_p177, main_1_p178, main_1_p179, main_1_p180, main_1_p181, main_1_p182, main_1_p183, main_1_p184, main_1_p185, main_1_p186, main_1_p187, main_1_p188, main_1_p189, main_1_p190, main_1_p191, main_1_p192, main_1_p193, main_1_p194, main_1_p195, main_1_p196, main_1_p197, main_1_p198, main_1_p199, main_1_p200, main_1_p201, main_1_p202, main_1_p203, main_1_p204, main_1_p205, main_1_p206, main_1_p207, main_1_p208, main_1_p209, main_1_p210, main_1_p211, main_1_p212, main_1_p213, main_1_p214, main_1_p215, main_1_p216, main_1_p217, main_1_p218, main_1_p219, main_1_p220, main_1_p221, main_1_p222, main_1_p223, main_1_p224, main_1_p225, main_1_p226, main_1_p227, main_1_p228, main_1_p229, main_1_p230, main_1_p231, main_1_p232, main_1_p233, main_1_p234, main_1_p235, main_1_p236, main_1_p237, main_1_p238, main_1_p239, main_1_p240, main_1_p241, main_1_p242, main_1_p243, main_1_p244, main_1_p245, main_1_p246, main_1_p247, main_1_p248, main_1_p249, main_1_p250, main_1_p251, main_1_p252, main_1_p253, main_1_p254, main_1_p255, main_1_p256, main_1_p257, main_1_p258, main_1_p259, main_1_p260, main_1_p261, main_1_p262, main_1_p263, main_1_p264, main_1_p265, main_1_p266, main_1_p267, main_1_p268, main_1_p269, main_1_p270, main_1_p271, main_1_p272, main_1_p273, main_1_p274, main_1_p275, main_1_p276, main_1_p277, main_1_p278, main_1_p279, main_1_p280, main_1_p281, main_1_p282, main_1_p283, main_1_p284, main_1_p285, main_1_p286, main_1_p287, main_1_p288, main_1_p289, main_1_p290, main_1_p291, main_1_p292, main_1_p293, main_1_p294, main_1_p295, main_1_p296, main_1_p297, main_1_p298, main_1_p299, main_1_p300, main_1_p301, main_1_p302, main_1_p303, main_1_p304, main_1_p305, main_1_p306, main_1_p307, main_1_p308, main_1_p309, main_1_p310, main_1_p311, main_1_p312, main_1_p313, main_1_p314, main_1_p315, main_1_p316, main_1_p317, main_1_p318, main_1_p319, main_1_p320, main_1_p321, main_1_p322, main_1_p323, main_1_p324, main_1_p325, main_1_p326, main_1_p327, main_1_p328, main_1_p329, main_1_p330, main_1_p331, main_1_p332, main_1_p333, main_1_p334, main_1_p335, main_1_p336, main_1_p337, main_1_p338, main_1_p339, main_1_p340, main_1_p341, main_1_p342, main_1_p343, main_1_p344, main_1_p345, main_1_p346, main_1_p347, main_1_p348, main_1_p349, main_1_p350, main_1_p351, main_1_p352, main_1_p353, main_1_p354, main_1_p355, main_1_p356, main_1_p357, main_1_p358, main_1_p359, main_1_p360, main_1_p361, K2CLK, main_1_p363, main_1_p364, main_1_p365, main_1_p366, main_1_p367, main_1_p368, main_1_p369, main_1_p370, K2RST, main_1_p372, main_1_p373, main_1_p374, main_1_p375, main_1_p376, main_1_p377, main_1_p378, main_1_p379, main_1_p380, main_1_p381, main_1_p382, main_1_p383, main_1_p384, main_1_p385, main_1_p386, main_1_p387, main_1_p388, main_1_p389, main_1_p390, main_1_p391, main_1_p392, main_1_p393, main_1_p394, main_1_p395, main_1_p396, main_1_p397, main_1_p398, main_1_p399, main_1_p400, main_1_p401, main_1_p402, main_1_p403, main_1_p404, main_1_p405, main_1_p406, main_1_p407, main_1_p408, main_1_p409, main_1_p410, main_1_p411, main_1_p412, main_1_p413, main_1_p414, main_1_p415, main_1_p416, main_1_p417, main_1_p418, main_1_p419, K2DATA, main_1_p421, main_1_p422, main_1_p423, main_1_p424, main_1_p425, main_1_p426, main_1_p427, main_1_p428, main_1_p429, main_1_p430, main_1_p431, main_1_p432, main_1_p433, main_1_p434, main_1_p435, main_1_p436, main_1_p437, main_1_p438, main_1_p439, main_1_p440, main_1_p441, main_1_p442, main_1_p443, main_1_p444, main_1_p445, main_1_p446, main_1_p447, main_1_p448, main_1_p449, main_1_p450, main_1_p451, main_1_p452, main_1_p453, main_1_p454, main_1_p455, main_1_p456, main_1_p457, main_1_p458, main_1_p459, main_1_p460, main_1_p461, main_1_p462, main_1_p463, main_1_p464, main_1_p465, main_1_p466, main_1_p467, main_1_p468, main_1_p469, main_1_p470, main_1_p471, main_1_p472, main_1_p473, main_1_p474, main_1_p475, main_1_p476, main_1_p477, main_1_p478, main_1_p479, main_1_p480, main_1_p481, main_1_p482, main_1_p483, main_1_p484, main_1_p485, main_1_p486, main_1_p487, main_1_p488, main_1_p489, main_1_p490, main_1_p491, main_1_p492, main_1_p493, main_1_p494, main_1_p495, main_1_p496, main_1_p497, main_1_p498, in_1, in_2
  DotMatrix #(.matrixcols(30), .matrixrows(30), .persist(500)) dotmatrix_1 (
    .col0(main_1_p1), .col1(main_1_p5), .col2(main_1_p9), .col3(main_1_p13), .col4(main_1_p17),
    .col5(main_1_p21), .col6(main_1_p25), .col7(main_1_p29), .col8(main_1_p33), .col9(main_1_p37),
    .col10(main_1_p41), .col11(main_1_p45), .col12(main_1_p49), .col13(main_1_p53), .col14(main_1_p57),
    .col15(main_1_p61), .col16(main_1_p65), .col17(main_1_p69), .col18(main_1_p73), .col19(main_1_p77),
    .col20(main_1_p81), .col21(main_1_p85), .col22(main_1_p90), .col23(main_1_p94), .col24(main_1_p99),
    .col25(main_1_p103), .col26(main_1_p107), .col27(main_1_p111), .col28(main_1_p115), .col29(main_1_p119));
  DotMatrix #(.matrixcols(30), .matrixrows(30), .persist(500)) dotmatrix_2 (
    .col0(main_1_p2), .col1(main_1_p6), .col2(main_1_p10), .col3(main_1_p14), .col4(main_1_p18),
    .col5(main_1_p22), .col6(main_1_p26), .col7(main_1_p30), .col8(main_1_p34), .col9(main_1_p38),
    .col10(main_1_p42), .col11(main_1_p46), .col12(main_1_p50), .col13(main_1_p54), .col14(main_1_p58),
    .col15(main_1_p62), .col16(main_1_p66), .col17(main_1_p70), .col18(main_1_p74), .col19(main_1_p78),
    .col20(main_1_p82), .col21(main_1_p86), .col22(main_1_p91), .col23(main_1_p95), .col24(main_1_p100),
    .col25(main_1_p104), .col26(main_1_p108), .col27(main_1_p112), .col28(main_1_p116), .col29(main_1_p120));
  DotMatrix #(.matrixcols(30), .matrixrows(30), .persist(500)) dotmatrix_3 (
    .col0(main_1_p3), .col1(main_1_p7), .col2(main_1_p11), .col3(main_1_p15), .col4(main_1_p19),
    .col5(main_1_p23), .col6(main_1_p27), .col7(main_1_p31), .col8(main_1_p35), .col9(main_1_p39),
    .col10(main_1_p43), .col11(main_1_p47), .col12(main_1_p51), .col13(main_1_p55), .col14(main_1_p59),
    .col15(main_1_p63), .col16(main_1_p67), .col17(main_1_p71), .col18(main_1_p75), .col19(main_1_p79),
    .col20(main_1_p83), .col21(main_1_p88), .col22(main_1_p92), .col23(main_1_p97), .col24(main_1_p101),
    .col25(main_1_p105), .col26(main_1_p109), .col27(main_1_p113), .col28(main_1_p117), .col29(main_1_p121));
  DotMatrix #(.matrixcols(30), .matrixrows(30), .persist(500)) dotmatrix_4 (
    .col0(main_1_p4), .col1(main_1_p8), .col2(main_1_p12), .col3(main_1_p16), .col4(main_1_p20),
    .col5(main_1_p24), .col6(main_1_p28), .col7(main_1_p32), .col8(main_1_p36), .col9(main_1_p40),
    .col10(main_1_p44), .col11(main_1_p48), .col12(main_1_p52), .col13(main_1_p56), .col14(main_1_p60),
    .col15(main_1_p64), .col16(main_1_p68), .col17(main_1_p72), .col18(main_1_p76), .col19(main_1_p80),
    .col20(main_1_p84), .col21(main_1_p89), .col22(main_1_p93), .col23(main_1_p98), .col24(main_1_p102),
    .col25(main_1_p106), .col26(main_1_p110), .col27(main_1_p114), .col28(main_1_p118), .col29(main_1_p122));
  DotMatrix #(.matrixcols(30), .matrixrows(30), .persist(500)) dotmatrix_5 (
    .col0(main_1_p123), .col1(main_1_p127), .col2(main_1_p131), .col3(main_1_p135), .col4(main_1_p139),
    .col5(main_1_p143), .col6(main_1_p148), .col7(main_1_p152), .col8(main_1_p156), .col9(main_1_p160),
    .col10(main_1_p164), .col11(main_1_p168), .col12(main_1_p172), .col13(main_1_p176), .col14(main_1_p180),
    .col15(main_1_p184), .col16(main_1_p188), .col17(main_1_p192), .col18(main_1_p196), .col19(main_1_p200),
    .col20(main_1_p204), .col21(main_1_p208), .col22(main_1_p212), .col23(main_1_p216), .col24(main_1_p220),
    .col25(main_1_p224), .col26(main_1_p228), .col27(main_1_p232), .col28(main_1_p236), .col29(main_1_p240));
  DotMatrix #(.matrixcols(30), .matrixrows(30), .persist(500)) dotmatrix_6 (
    .col0(main_1_p124), .col1(main_1_p128), .col2(main_1_p132), .col3(main_1_p136), .col4(main_1_p140),
    .col5(main_1_p144), .col6(main_1_p149), .col7(main_1_p153), .col8(main_1_p157), .col9(main_1_p161),
    .col10(main_1_p165), .col11(main_1_p169), .col12(main_1_p173), .col13(main_1_p177), .col14(main_1_p181),
    .col15(main_1_p185), .col16(main_1_p189), .col17(main_1_p193), .col18(main_1_p197), .col19(main_1_p201),
    .col20(main_1_p205), .col21(main_1_p209), .col22(main_1_p213), .col23(main_1_p217), .col24(main_1_p221),
    .col25(main_1_p225), .col26(main_1_p229), .col27(main_1_p233), .col28(main_1_p237), .col29(main_1_p241));
  DotMatrix #(.matrixcols(30), .matrixrows(30), .persist(500)) dotmatrix_7 (
    .col0(main_1_p125), .col1(main_1_p129), .col2(main_1_p133), .col3(main_1_p137), .col4(main_1_p141),
    .col5(main_1_p146), .col6(main_1_p150), .col7(main_1_p154), .col8(main_1_p158), .col9(main_1_p162),
    .col10(main_1_p166), .col11(main_1_p170), .col12(main_1_p174), .col13(main_1_p178), .col14(main_1_p182),
    .col15(main_1_p186), .col16(main_1_p190), .col17(main_1_p194), .col18(main_1_p198), .col19(main_1_p202),
    .col20(main_1_p206), .col21(main_1_p210), .col22(main_1_p214), .col23(main_1_p218), .col24(main_1_p222),
    .col25(main_1_p226), .col26(main_1_p230), .col27(main_1_p234), .col28(main_1_p238), .col29(main_1_p242));
  DotMatrix #(.matrixcols(30), .matrixrows(30), .persist(500)) dotmatrix_8 (
    .col0(main_1_p126), .col1(main_1_p130), .col2(main_1_p134), .col3(main_1_p138), .col4(main_1_p142),
    .col5(main_1_p147), .col6(main_1_p151), .col7(main_1_p155), .col8(main_1_p159), .col9(main_1_p163),
    .col10(main_1_p167), .col11(main_1_p171), .col12(main_1_p175), .col13(main_1_p179), .col14(main_1_p183),
    .col15(main_1_p187), .col16(main_1_p191), .col17(main_1_p195), .col18(main_1_p199), .col19(main_1_p203),
    .col20(main_1_p207), .col21(main_1_p211), .col22(main_1_p215), .col23(main_1_p219), .col24(main_1_p223),
    .col25(main_1_p227), .col26(main_1_p231), .col27(main_1_p235), .col28(main_1_p239), .col29(main_1_p243));
  _7_Segment_Display u_7_segment_display_1 (
    .g(main_2_out_10), .f(main_2_out_11), .a(main_2_out_12), .b(main_2_out_13), .e(main_2_out_26),
    .d(main_2_out_27), .c(main_2_out_28), .dp(main_2_out_29));
  secs_to_score_main main_2 (
    .SECS_IPT(main_1_p244), .out_10(main_2_out_10), .out_11(main_2_out_11), .out_12(main_2_out_12),
    .out_13(main_2_out_13), .out_26(main_2_out_26), .out_27(main_2_out_27), .out_28(main_2_out_28),
    .out_29(main_2_out_29), .out_14(main_2_out_14), .out_15(main_2_out_15), .out_16(main_2_out_16),
    .out_17(main_2_out_17), .out_30(main_2_out_30), .out_31(main_2_out_31), .out_32(main_2_out_32),
    .out_33(main_2_out_33), .out_2(main_2_out_2), .out_3(main_2_out_3), .out_4(main_2_out_4),
    .out_5(main_2_out_5), .out_18(main_2_out_18), .out_19(main_2_out_19), .out_20(main_2_out_20),
    .out_21(main_2_out_21), .out_6(main_2_out_6), .out_7(main_2_out_7), .out_8(main_2_out_8),
    .out_9(main_2_out_9), .out_22(main_2_out_22), .out_23(main_2_out_23), .out_24(main_2_out_24),
    .out_25(main_2_out_25));
  secs_to_score_main main_3 (
    .SECS_IPT(main_1_p245), .out_10(main_3_out_10), .out_11(main_3_out_11), .out_12(main_3_out_12),
    .out_13(main_3_out_13), .out_26(main_3_out_26), .out_27(main_3_out_27), .out_28(main_3_out_28),
    .out_29(main_3_out_29), .out_14(main_3_out_14), .out_15(main_3_out_15), .out_16(main_3_out_16),
    .out_17(main_3_out_17), .out_30(main_3_out_30), .out_31(main_3_out_31), .out_32(main_3_out_32),
    .out_33(main_3_out_33), .out_2(main_3_out_2), .out_3(main_3_out_3), .out_4(main_3_out_4),
    .out_5(main_3_out_5), .out_18(main_3_out_18), .out_19(main_3_out_19), .out_20(main_3_out_20),
    .out_21(main_3_out_21), .out_6(main_3_out_6), .out_7(main_3_out_7), .out_8(main_3_out_8),
    .out_9(main_3_out_9), .out_22(main_3_out_22), .out_23(main_3_out_23), .out_24(main_3_out_24),
    .out_25(main_3_out_25));
  _7_Segment_Display u_7_segment_display_2 (
    .g(main_3_out_10), .f(main_3_out_11), .a(main_3_out_12), .b(main_3_out_13), .e(main_3_out_26),
    .d(main_3_out_27), .c(main_3_out_28), .dp(main_3_out_29));
  _7_Segment_Display u_7_segment_display_3 (
    .g(main_4_out_10), .f(main_4_out_11), .a(main_4_out_12), .b(main_4_out_13), .e(main_4_out_26),
    .d(main_4_out_27), .c(main_4_out_28), .dp(main_4_out_29));
  secs_to_score_main main_4 (
    .SECS_IPT(main_1_p246), .out_10(main_4_out_10), .out_11(main_4_out_11), .out_12(main_4_out_12),
    .out_13(main_4_out_13), .out_26(main_4_out_26), .out_27(main_4_out_27), .out_28(main_4_out_28),
    .out_29(main_4_out_29), .out_14(main_4_out_14), .out_15(main_4_out_15), .out_16(main_4_out_16),
    .out_17(main_4_out_17), .out_30(main_4_out_30), .out_31(main_4_out_31), .out_32(main_4_out_32),
    .out_33(main_4_out_33), .out_2(main_4_out_2), .out_3(main_4_out_3), .out_4(main_4_out_4),
    .out_5(main_4_out_5), .out_18(main_4_out_18), .out_19(main_4_out_19), .out_20(main_4_out_20),
    .out_21(main_4_out_21), .out_6(main_4_out_6), .out_7(main_4_out_7), .out_8(main_4_out_8),
    .out_9(main_4_out_9), .out_22(main_4_out_22), .out_23(main_4_out_23), .out_24(main_4_out_24),
    .out_25(main_4_out_25));
  secs_to_score_main main_5 (
    .SECS_IPT(main_1_p247), .out_10(main_5_out_10), .out_11(main_5_out_11), .out_12(main_5_out_12),
    .out_13(main_5_out_13), .out_26(main_5_out_26), .out_27(main_5_out_27), .out_28(main_5_out_28),
    .out_29(main_5_out_29), .out_14(main_5_out_14), .out_15(main_5_out_15), .out_16(main_5_out_16),
    .out_17(main_5_out_17), .out_30(main_5_out_30), .out_31(main_5_out_31), .out_32(main_5_out_32),
    .out_33(main_5_out_33), .out_2(main_5_out_2), .out_3(main_5_out_3), .out_4(main_5_out_4),
    .out_5(main_5_out_5), .out_18(main_5_out_18), .out_19(main_5_out_19), .out_20(main_5_out_20),
    .out_21(main_5_out_21), .out_6(main_5_out_6), .out_7(main_5_out_7), .out_8(main_5_out_8),
    .out_9(main_5_out_9), .out_22(main_5_out_22), .out_23(main_5_out_23), .out_24(main_5_out_24),
    .out_25(main_5_out_25));
  _7_Segment_Display u_7_segment_display_4 (
    .g(main_5_out_10), .f(main_5_out_11), .a(main_5_out_12), .b(main_5_out_13), .e(main_5_out_26),
    .d(main_5_out_27), .c(main_5_out_28), .dp(main_5_out_29));
  _7_Segment_Display u_7_segment_display_5 (
    .g(main_2_out_2), .f(main_2_out_3), .a(main_2_out_4), .b(main_2_out_5), .e(main_2_out_18),
    .d(main_2_out_19), .c(main_2_out_20), .dp(main_2_out_21));
  _7_Segment_Display u_7_segment_display_6 (
    .g(main_2_out_14), .f(main_2_out_15), .a(main_2_out_16), .b(main_2_out_17), .e(main_2_out_30),
    .d(main_2_out_31), .c(main_2_out_32), .dp(main_2_out_33));
  _7_Segment_Display u_7_segment_display_7 (
    .g(main_3_out_14), .f(main_3_out_15), .a(main_3_out_16), .b(main_3_out_17), .e(main_3_out_30),
    .d(main_3_out_31), .c(main_3_out_32), .dp(main_3_out_33));
  _7_Segment_Display u_7_segment_display_8 (
    .g(main_3_out_2), .f(main_3_out_3), .a(main_3_out_4), .b(main_3_out_5), .e(main_3_out_18),
    .d(main_3_out_19), .c(main_3_out_20), .dp(main_3_out_21));
  _7_Segment_Display u_7_segment_display_9 (
    .g(main_4_out_2), .f(main_4_out_3), .a(main_4_out_4), .b(main_4_out_5), .e(main_4_out_18),
    .d(main_4_out_19), .c(main_4_out_20), .dp(main_4_out_21));
  _7_Segment_Display u_7_segment_display_10 (
    .g(main_4_out_14), .f(main_4_out_15), .a(main_4_out_16), .b(main_4_out_17), .e(main_4_out_30),
    .d(main_4_out_31), .c(main_4_out_32), .dp(main_4_out_33));
  _7_Segment_Display u_7_segment_display_11 (
    .g(main_5_out_14), .f(main_5_out_15), .a(main_5_out_16), .b(main_5_out_17), .e(main_5_out_30),
    .d(main_5_out_31), .c(main_5_out_32), .dp(main_5_out_33));
  _7_Segment_Display u_7_segment_display_12 (
    .g(main_5_out_2), .f(main_5_out_3), .a(main_5_out_4), .b(main_5_out_5), .e(main_5_out_18),
    .d(main_5_out_19), .c(main_5_out_20), .dp(main_5_out_21));
  DotMatrix #(.matrixcols(8), .matrixrows(5)) dotmatrix_9 (
    .col0(main_1_p248), .col1(main_1_p249), .col2(main_1_p250), .col3(main_1_p251), .col4(main_1_p252),
    .col5(main_1_p253), .col6(main_1_p254), .col7(main_1_p255));
  _7_Segment_Display u_7_segment_display_13 (
    .g(main_2_out_6), .f(main_2_out_7), .a(main_2_out_8), .b(main_2_out_9), .e(main_2_out_22),
    .d(main_2_out_23), .c(main_2_out_24), .dp(main_2_out_25));
  _7_Segment_Display u_7_segment_display_14 (
    .g(main_3_out_6), .f(main_3_out_7), .a(main_3_out_8), .b(main_3_out_9), .e(main_3_out_22),
    .d(main_3_out_23), .c(main_3_out_24), .dp(main_3_out_25));
  _7_Segment_Display u_7_segment_display_15 (
    .g(main_4_out_6), .f(main_4_out_7), .a(main_4_out_8), .b(main_4_out_9), .e(main_4_out_22),
    .d(main_4_out_23), .c(main_4_out_24), .dp(main_4_out_25));
  _7_Segment_Display u_7_segment_display_16 (
    .g(main_5_out_6), .f(main_5_out_7), .a(main_5_out_8), .b(main_5_out_9), .e(main_5_out_22),
    .d(main_5_out_23), .c(main_5_out_24), .dp(main_5_out_25));
  DotMatrix #(.matrixcols(30), .matrixrows(30), .persist(500)) dotmatrix_10 (
    .col0(main_1_p256), .col1(main_1_p260), .col2(main_1_p264), .col3(main_1_p268), .col4(main_1_p272),
    .col5(main_1_p276), .col6(main_1_p280), .col7(main_1_p284), .col8(main_1_p288), .col9(main_1_p292),
    .col10(main_1_p296), .col11(main_1_p300), .col12(main_1_p304), .col13(main_1_p308), .col14(main_1_p312),
    .col15(main_1_p316), .col16(main_1_p320), .col17(main_1_p324), .col18(main_1_p328), .col19(main_1_p332),
    .col20(main_1_p336), .col21(main_1_p340), .col22(main_1_p344), .col23(main_1_p348), .col24(main_1_p352),
    .col25(main_1_p356), .col26(main_1_p360), .col27(main_1_p365), .col28(main_1_p369), .col29(main_1_p374));
  DotMatrix #(.matrixcols(30), .matrixrows(30), .persist(500)) dotmatrix_11 (
    .col0(main_1_p257), .col1(main_1_p261), .col2(main_1_p265), .col3(main_1_p269), .col4(main_1_p273),
    .col5(main_1_p277), .col6(main_1_p281), .col7(main_1_p285), .col8(main_1_p289), .col9(main_1_p293),
    .col10(main_1_p297), .col11(main_1_p301), .col12(main_1_p305), .col13(main_1_p309), .col14(main_1_p313),
    .col15(main_1_p317), .col16(main_1_p321), .col17(main_1_p325), .col18(main_1_p329), .col19(main_1_p333),
    .col20(main_1_p337), .col21(main_1_p341), .col22(main_1_p345), .col23(main_1_p349), .col24(main_1_p353),
    .col25(main_1_p357), .col26(main_1_p361), .col27(main_1_p366), .col28(main_1_p370), .col29(main_1_p375));
  DotMatrix #(.matrixcols(30), .matrixrows(30), .persist(500)) dotmatrix_12 (
    .col0(main_1_p258), .col1(main_1_p262), .col2(main_1_p266), .col3(main_1_p270), .col4(main_1_p274),
    .col5(main_1_p278), .col6(main_1_p282), .col7(main_1_p286), .col8(main_1_p290), .col9(main_1_p294),
    .col10(main_1_p298), .col11(main_1_p302), .col12(main_1_p306), .col13(main_1_p310), .col14(main_1_p314),
    .col15(main_1_p318), .col16(main_1_p322), .col17(main_1_p326), .col18(main_1_p330), .col19(main_1_p334),
    .col20(main_1_p338), .col21(main_1_p342), .col22(main_1_p346), .col23(main_1_p350), .col24(main_1_p354),
    .col25(main_1_p358), .col26(main_1_p363), .col27(main_1_p367), .col28(main_1_p372), .col29(main_1_p376));
  DotMatrix #(.matrixcols(30), .matrixrows(30), .persist(500)) dotmatrix_13 (
    .col0(main_1_p259), .col1(main_1_p263), .col2(main_1_p267), .col3(main_1_p271), .col4(main_1_p275),
    .col5(main_1_p279), .col6(main_1_p283), .col7(main_1_p287), .col8(main_1_p291), .col9(main_1_p295),
    .col10(main_1_p299), .col11(main_1_p303), .col12(main_1_p307), .col13(main_1_p311), .col14(main_1_p315),
    .col15(main_1_p319), .col16(main_1_p323), .col17(main_1_p327), .col18(main_1_p331), .col19(main_1_p335),
    .col20(main_1_p339), .col21(main_1_p343), .col22(main_1_p347), .col23(main_1_p351), .col24(main_1_p355),
    .col25(main_1_p359), .col26(main_1_p364), .col27(main_1_p368), .col28(main_1_p373), .col29(main_1_p377));
  DotMatrix #(.matrixcols(30), .matrixrows(30), .persist(500)) dotmatrix_14 (
    .col0(main_1_p378), .col1(main_1_p382), .col2(main_1_p386), .col3(main_1_p390), .col4(main_1_p394),
    .col5(main_1_p398), .col6(main_1_p402), .col7(main_1_p406), .col8(main_1_p410), .col9(main_1_p414),
    .col10(main_1_p418), .col11(main_1_p423), .col12(main_1_p427), .col13(main_1_p431), .col14(main_1_p435),
    .col15(main_1_p439), .col16(main_1_p443), .col17(main_1_p447), .col18(main_1_p451), .col19(main_1_p455),
    .col20(main_1_p459), .col21(main_1_p463), .col22(main_1_p467), .col23(main_1_p471), .col24(main_1_p475),
    .col25(main_1_p479), .col26(main_1_p483), .col27(main_1_p487), .col28(main_1_p491), .col29(main_1_p495));
  DotMatrix #(.matrixcols(30), .matrixrows(30), .persist(500)) dotmatrix_15 (
    .col0(main_1_p379), .col1(main_1_p383), .col2(main_1_p387), .col3(main_1_p391), .col4(main_1_p395),
    .col5(main_1_p399), .col6(main_1_p403), .col7(main_1_p407), .col8(main_1_p411), .col9(main_1_p415),
    .col10(main_1_p419), .col11(main_1_p424), .col12(main_1_p428), .col13(main_1_p432), .col14(main_1_p436),
    .col15(main_1_p440), .col16(main_1_p444), .col17(main_1_p448), .col18(main_1_p452), .col19(main_1_p456),
    .col20(main_1_p460), .col21(main_1_p464), .col22(main_1_p468), .col23(main_1_p472), .col24(main_1_p476),
    .col25(main_1_p480), .col26(main_1_p484), .col27(main_1_p488), .col28(main_1_p492), .col29(main_1_p496));
  DotMatrix #(.matrixcols(30), .matrixrows(30), .persist(500)) dotmatrix_16 (
    .col0(main_1_p380), .col1(main_1_p384), .col2(main_1_p388), .col3(main_1_p392), .col4(main_1_p396),
    .col5(main_1_p400), .col6(main_1_p404), .col7(main_1_p408), .col8(main_1_p412), .col9(main_1_p416),
    .col10(main_1_p421), .col11(main_1_p425), .col12(main_1_p429), .col13(main_1_p433), .col14(main_1_p437),
    .col15(main_1_p441), .col16(main_1_p445), .col17(main_1_p449), .col18(main_1_p453), .col19(main_1_p457),
    .col20(main_1_p461), .col21(main_1_p465), .col22(main_1_p469), .col23(main_1_p473), .col24(main_1_p477),
    .col25(main_1_p481), .col26(main_1_p485), .col27(main_1_p489), .col28(main_1_p493), .col29(main_1_p497));
  DotMatrix #(.matrixcols(30), .matrixrows(30), .persist(500)) dotmatrix_17 (
    .col0(main_1_p381), .col1(main_1_p385), .col2(main_1_p389), .col3(main_1_p393), .col4(main_1_p397),
    .col5(main_1_p401), .col6(main_1_p405), .col7(main_1_p409), .col8(main_1_p413), .col9(main_1_p417),
    .col10(main_1_p422), .col11(main_1_p426), .col12(main_1_p430), .col13(main_1_p434), .col14(main_1_p438),
    .col15(main_1_p442), .col16(main_1_p446), .col17(main_1_p450), .col18(main_1_p454), .col19(main_1_p458),
    .col20(main_1_p462), .col21(main_1_p466), .col22(main_1_p470), .col23(main_1_p474), .col24(main_1_p478),
    .col25(main_1_p482), .col26(main_1_p486), .col27(main_1_p490), .col28(main_1_p494), .col29(main_1_p498));
  Keyboard keyboard_1 (.clk(K1CLK), .clr(K1RST), .data(K1DATA));  // open: re, avail
  Keyboard keyboard_2 (.clk(K2CLK), .clr(K2RST), .data(K2DATA));  // open: re, avail
endmodule
