// Logisim project not_hit_ram_storage.circ as structural Verilog: 1 circuit, main circuit main
module main (
  input  IF_1__save_input,
  input  CLR,
  input  [3:0] X,
  input  [3:0] Y,
  input  CLK,
  input  in_6,
  output [3:0] X_2,
  output [3:0] Y_2
);

  wire _2nd_MEM_END, and_1_out, and_3_out, CLK_t, comparator_1_eq, comparator_2_lt, controlled_buffer_1_out,
       HIT_REGISTER, main_4_out_3, MEM_END, MIN_1_THE_SAME, not_1_out, not_hit___0, or_1_out, or_2_out,
       or_3_out, STORE, TEST_PASSED;
  wire [7:0] ADDRESS, DATA_TO_CHECK, ram_1_data, STABLE_COUNTER_q;

  not not_1 (not_1_out, MIN_1_THE_SAME);
  SRlatch_main main_1 (.RESTET(STORE), .SET(IF_1__save_input), .Q(HIT_REGISTER));
  Comparator comparator_1 (.a(DATA_TO_CHECK), .b({Y_2, X_2}), .eq(comparator_1_eq));  // open: gt, lt
  Pull_Resistor pull_resistor_1 (.node(comparator_1_eq));
  or or_1 (or_1_out, _2nd_MEM_END, CLR);
  Counter #(.width(1), .max('h1), .ongoal("stay")) counter_1 (
    .carry(_2nd_MEM_END), .clk(and_1_out), .clr(or_2_out));  // open: load, D, count, Q
  and and_1 (and_1_out, MEM_END, TEST_PASSED);
  or or_2 (or_2_out, _2nd_MEM_END, CLR);
  and and_2 (STORE, _2nd_MEM_END, TEST_PASSED);
  SRlatch_main main_2 (.RESTET(or_1_out), .SET(comparator_1_eq), .Q(MIN_1_THE_SAME));
  and and_3 (and_3_out, HIT_REGISTER, MEM_END, not_1_out);
  tick_main main_3 (.in_1(CLK_t), .in_2(and_3_out), .out_3(TEST_PASSED));
  Clock clock_1 (.out(CLK_t));
  Counter #(.width(1), .max('h1), .ongoal("stay")) count_form_0 (
    .carry(not_hit___0), .clk(IF_1__save_input), .clr(CLR));  // open: load, D, count, Q
  Counter #(.max('h90)) STABLE_COUNTER (
    .Q(STABLE_COUNTER_q), .clk(controlled_buffer_1_out), .clr(CLR));  // open: load, D, count, carry
  assign controlled_buffer_1_out = not_hit___0 ? TEST_PASSED : 1'bz;  // Controlled_Buffer controlled_buffer_1
  Register register_1 (.D({Y, X}), .Q(DATA_TO_CHECK), .clk(IF_1__save_input), .clr(CLR));  // open: en
  Comparator comparator_2 (.a(STABLE_COUNTER_q), .b(ADDRESS), .eq(MEM_END), .lt(comparator_2_lt));  // open: gt
  RAM #(.bus("separate")) ram_1 (
    .addr(ADDRESS), .din(DATA_TO_CHECK), .data(ram_1_data), .str(STORE), .clk(CLK_t), .ld(1'b1), .clr(CLR));  // open: sel
  tick_main main_4 (.in_1(CLK_t), .in_2(MEM_END), .out_3(main_4_out_3));
  assign {Y_2, X_2} = not_hit___0 ? ram_1_data : 8'bz;  // Controlled_Buffer controlled_buffer_2
  or or_3 (or_3_out, main_4_out_3, comparator_2_lt, IF_1__save_input, CLR);
  Counter #(.max('h90)) UNSTABLE_COUNTER (.Q(ADDRESS), .clk(CLK_t), .clr(or_3_out));  // open: load, D, count, carry

  // Other names for the same wires on the sheet: CHECKED = in_6; CURRENT_MEM_OUT[7:0] = {Y_2, X_2};
  //   nHIT = IF_1__save_input
endmodule
