// Logisim project przesuwanko.circ as structural Verilog: 1 circuit, main circuit main
module main (
);

  wire and_1_out, and_2_out, CLK, DOWN, f_CLK_2, LEFT, not_1_out, or_1_out, or_2_out, RIGHT, SCREEN_X,
       SCREEN_Y, undriven, UP;
  wire [2:0] counter_1_q, counter_3_q;
  wire [4:0] adder_1_out, BL, BR, multiplier_2_out, rom_1_data, TL, TR;
  wire [5:0] bit_extender_1_out, multiplier_1_out, XPOS, YPOS;
  wire [6:0] keyboard_1_data;
  wire [31:0] bit_extender_2_out, BL_DATA, BR_DATA, controlled_buffer_1_out, demultiplexer_3_out0,
       demultiplexer_3_out1, demultiplexer_3_out2, demultiplexer_3_out3, demultiplexer_3_out4,
       demultiplexer_3_out5, demultiplexer_3_out6, demultiplexer_3_out7, demultiplexer_3_out8,
       demultiplexer_3_out9, demultiplexer_3_out10, demultiplexer_3_out11, demultiplexer_3_out12,
       demultiplexer_3_out13, demultiplexer_3_out14, demultiplexer_3_out15, demultiplexer_3_out16,
       demultiplexer_3_out17, demultiplexer_3_out18, demultiplexer_3_out19, demultiplexer_3_out20,
       demultiplexer_3_out21, demultiplexer_3_out22, demultiplexer_3_out23, demultiplexer_3_out24,
       demultiplexer_3_out25, demultiplexer_3_out26, demultiplexer_3_out27, demultiplexer_3_out28,
       demultiplexer_3_out29, demultiplexer_3_out30, demultiplexer_3_out31, demultiplexer_4_out0,
       demultiplexer_4_out1, demultiplexer_4_out2, demultiplexer_4_out3, demultiplexer_4_out4,
       demultiplexer_4_out5, demultiplexer_4_out6, demultiplexer_4_out7, demultiplexer_4_out8,
       demultiplexer_4_out9, demultiplexer_4_out10, demultiplexer_4_out11, demultiplexer_4_out12,
       demultiplexer_4_out13, demultiplexer_4_out14, demultiplexer_4_out15, demultiplexer_4_out16,
       demultiplexer_4_out17, demultiplexer_4_out18, demultiplexer_4_out19, demultiplexer_4_out20,
       demultiplexer_4_out21, demultiplexer_4_out22, demultiplexer_4_out23, demultiplexer_4_out24,
       demultiplexer_4_out25, demultiplexer_4_out26, demultiplexer_4_out27, demultiplexer_4_out28,
       demultiplexer_4_out29, demultiplexer_4_out30, demultiplexer_4_out31, demultiplexer_5_out0,
       demultiplexer_5_out1, demultiplexer_5_out2, demultiplexer_5_out3, demultiplexer_5_out4,
       demultiplexer_5_out5, demultiplexer_5_out6, demultiplexer_5_out7, demultiplexer_5_out8,
       demultiplexer_5_out9, demultiplexer_5_out10, demultiplexer_5_out11, demultiplexer_5_out12,
       demultiplexer_5_out13, demultiplexer_5_out14, demultiplexer_5_out15, demultiplexer_5_out16,
       demultiplexer_5_out17, demultiplexer_5_out18, demultiplexer_5_out19, demultiplexer_5_out20,
       demultiplexer_5_out21, demultiplexer_5_out22, demultiplexer_5_out23, demultiplexer_5_out24,
       demultiplexer_5_out25, demultiplexer_5_out26, demultiplexer_5_out27, demultiplexer_5_out28,
       demultiplexer_5_out29, demultiplexer_5_out30, demultiplexer_5_out31, demultiplexer_6_out0,
       demultiplexer_6_out1, demultiplexer_6_out2, demultiplexer_6_out3, demultiplexer_6_out4,
       demultiplexer_6_out5, demultiplexer_6_out6, demultiplexer_6_out7, demultiplexer_6_out8,
       demultiplexer_6_out9, demultiplexer_6_out10, demultiplexer_6_out11, demultiplexer_6_out12,
       demultiplexer_6_out13, demultiplexer_6_out14, demultiplexer_6_out15, demultiplexer_6_out16,
       demultiplexer_6_out17, demultiplexer_6_out18, demultiplexer_6_out19, demultiplexer_6_out20,
       demultiplexer_6_out21, demultiplexer_6_out22, demultiplexer_6_out23, demultiplexer_6_out24,
       demultiplexer_6_out25, demultiplexer_6_out26, demultiplexer_6_out27, demultiplexer_6_out28,
       demultiplexer_6_out29, demultiplexer_6_out30, demultiplexer_6_out31, shifter_1_out, shifter_2_out,
       TL_DATA, TR_DATA;

  Clock u_CLK (.out(CLK));
  Counter #(.width(3), .max('h4)) counter_1 (.Q(counter_1_q), .clk(f_CLK_2));  // open: load, D, count, carry, clr
  Counter #(.width(1), .max('h1)) counter_2 (.carry(f_CLK_2), .clk(CLK));  // open: load, D, count, Q, clr
  Multiplier #(.width(6)) multiplier_1 (.a(XPOS), .b(6'b000101), .out(multiplier_1_out));  // open: cin, cout
  Counter #(.width(3), .max('h4)) counter_3 (.Q(counter_3_q), .clk(f_CLK_2));  // open: load, D, count, carry, clr
  assign bit_extender_1_out = {{3{1'b0}}, counter_3_q};  // Bit_Extender bit_extender_1
  Adder #(.width(6)) adder_1 (
    .a(multiplier_1_out), .b(bit_extender_1_out), .out({SCREEN_X, adder_1_out}));  // open: cin, cout
  ROM #(.addrWidth(3), .dataWidth(5)) rom_1 (.addr(counter_1_q), .data(rom_1_data));  // open: sel
  Demultiplexer #(.select(2), .width(5), .enable("false")) demultiplexer_1 (
    .out0(TL), .out1(TR), .out2(BL), .out3(BR), .in(adder_1_out), .sel({SCREEN_Y, SCREEN_X}));
  assign bit_extender_2_out = {{27{1'b0}}, rom_1_data};  // Bit_Extender bit_extender_2
  Multiplier #(.width(6)) multiplier_2 (
    .a(YPOS), .b(6'b000101), .out({SCREEN_Y, multiplier_2_out}));  // open: cin, cout
  Shifter #(.width(32)) shifter_1 (.in(bit_extender_2_out), .\dist (5'b11011), .out(shifter_1_out));
  not not_1 (not_1_out, f_CLK_2);
  Shifter #(.width(32), .shift("lr")) shifter_2 (.in(shifter_1_out), .\dist (multiplier_2_out), .out(shifter_2_out));
  assign controlled_buffer_1_out = not_1_out ? shifter_2_out : 32'bz;  // Controlled_Buffer controlled_buffer_1
  Pull_Resistor pull_resistor_1 (.node(controlled_buffer_1_out));
  Demultiplexer #(.select(2), .width(32), .enable("false")) demultiplexer_2 (
    .out0(TL_DATA), .out1(TR_DATA), .out2(BL_DATA), .out3(BR_DATA), .in(controlled_buffer_1_out),
    .sel({SCREEN_Y, SCREEN_X}));
  DotMatrix #(.matrixcols(32), .matrixrows(32), .persist(30)) dotmatrix_1 (
    .col0(demultiplexer_3_out0), .col1(demultiplexer_3_out1), .col2(demultiplexer_3_out2),
    .col3(demultiplexer_3_out3), .col4(demultiplexer_3_out4), .col5(demultiplexer_3_out5),
    .col6(demultiplexer_3_out6), .col7(demultiplexer_3_out7), .col8(demultiplexer_3_out8),
    .col9(demultiplexer_3_out9), .col10(demultiplexer_3_out10), .col11(demultiplexer_3_out11),
    .col12(demultiplexer_3_out12), .col13(demultiplexer_3_out13), .col14(demultiplexer_3_out14),
    .col15(demultiplexer_3_out15), .col16(demultiplexer_3_out16), .col17(demultiplexer_3_out17),
    .col18(demultiplexer_3_out18), .col19(demultiplexer_3_out19), .col20(demultiplexer_3_out20),
    .col21(demultiplexer_3_out21), .col22(demultiplexer_3_out22), .col23(demultiplexer_3_out23),
    .col24(demultiplexer_3_out24), .col25(demultiplexer_3_out25), .col26(demultiplexer_3_out26),
    .col27(demultiplexer_3_out27), .col28(demultiplexer_3_out28), .col29(demultiplexer_3_out29),
    .col30(demultiplexer_3_out30), .col31(demultiplexer_3_out31));
  DotMatrix #(.matrixcols(32), .matrixrows(32), .persist(30)) dotmatrix_2 (
    .col0(demultiplexer_4_out0), .col1(demultiplexer_4_out1), .col2(demultiplexer_4_out2),
    .col3(demultiplexer_4_out3), .col4(demultiplexer_4_out4), .col5(demultiplexer_4_out5),
    .col6(demultiplexer_4_out6), .col7(demultiplexer_4_out7), .col8(demultiplexer_4_out8),
    .col9(demultiplexer_4_out9), .col10(demultiplexer_4_out10), .col11(demultiplexer_4_out11),
    .col12(demultiplexer_4_out12), .col13(demultiplexer_4_out13), .col14(demultiplexer_4_out14),
    .col15(demultiplexer_4_out15), .col16(demultiplexer_4_out16), .col17(demultiplexer_4_out17),
    .col18(demultiplexer_4_out18), .col19(demultiplexer_4_out19), .col20(demultiplexer_4_out20),
    .col21(demultiplexer_4_out21), .col22(demultiplexer_4_out22), .col23(demultiplexer_4_out23),
    .col24(demultiplexer_4_out24), .col25(demultiplexer_4_out25), .col26(demultiplexer_4_out26),
    .col27(demultiplexer_4_out27), .col28(demultiplexer_4_out28), .col29(demultiplexer_4_out29),
    .col30(demultiplexer_4_out30), .col31(demultiplexer_4_out31));
  Demultiplexer #(.select(5), .width(32)) demultiplexer_3 (
    .out0(demultiplexer_3_out0), .out1(demultiplexer_3_out1), .out2(demultiplexer_3_out2),
    .out3(demultiplexer_3_out3), .out4(demultiplexer_3_out4), .out5(demultiplexer_3_out5),
    .out6(demultiplexer_3_out6), .out7(demultiplexer_3_out7), .out8(demultiplexer_3_out8),
    .out9(demultiplexer_3_out9), .out10(demultiplexer_3_out10), .out11(demultiplexer_3_out11),
    .out12(demultiplexer_3_out12), .out13(demultiplexer_3_out13), .out14(demultiplexer_3_out14),
    .out15(demultiplexer_3_out15), .out16(demultiplexer_3_out16), .out17(demultiplexer_3_out17),
    .out18(demultiplexer_3_out18), .out19(demultiplexer_3_out19), .out20(demultiplexer_3_out20),
    .out21(demultiplexer_3_out21), .out22(demultiplexer_3_out22), .out23(demultiplexer_3_out23),
    .out24(demultiplexer_3_out24), .out25(demultiplexer_3_out25), .out26(demultiplexer_3_out26),
    .out27(demultiplexer_3_out27), .out28(demultiplexer_3_out28), .out29(demultiplexer_3_out29),
    .out30(demultiplexer_3_out30), .out31(demultiplexer_3_out31), .in(TL_DATA), .sel(TL));  // open: en
  Demultiplexer #(.select(5), .width(32)) demultiplexer_4 (
    .out0(demultiplexer_4_out0), .out1(demultiplexer_4_out1), .out2(demultiplexer_4_out2),
    .out3(demultiplexer_4_out3), .out4(demultiplexer_4_out4), .out5(demultiplexer_4_out5),
    .out6(demultiplexer_4_out6), .out7(demultiplexer_4_out7), .out8(demultiplexer_4_out8),
    .out9(demultiplexer_4_out9), .out10(demultiplexer_4_out10), .out11(demultiplexer_4_out11),
    .out12(demultiplexer_4_out12), .out13(demultiplexer_4_out13), .out14(demultiplexer_4_out14),
    .out15(demultiplexer_4_out15), .out16(demultiplexer_4_out16), .out17(demultiplexer_4_out17),
    .out18(demultiplexer_4_out18), .out19(demultiplexer_4_out19), .out20(demultiplexer_4_out20),
    .out21(demultiplexer_4_out21), .out22(demultiplexer_4_out22), .out23(demultiplexer_4_out23),
    .out24(demultiplexer_4_out24), .out25(demultiplexer_4_out25), .out26(demultiplexer_4_out26),
    .out27(demultiplexer_4_out27), .out28(demultiplexer_4_out28), .out29(demultiplexer_4_out29),
    .out30(demultiplexer_4_out30), .out31(demultiplexer_4_out31), .in(BL_DATA), .sel(BL));  // open: en
  DotMatrix #(.matrixcols(32), .matrixrows(32), .persist(30)) dotmatrix_3 (
    .col0(demultiplexer_5_out0), .col1(demultiplexer_5_out1), .col2(demultiplexer_5_out2),
    .col3(demultiplexer_5_out3), .col4(demultiplexer_5_out4), .col5(demultiplexer_5_out5),
    .col6(demultiplexer_5_out6), .col7(demultiplexer_5_out7), .col8(demultiplexer_5_out8),
    .col9(demultiplexer_5_out9), .col10(demultiplexer_5_out10), .col11(demultiplexer_5_out11),
    .col12(demultiplexer_5_out12), .col13(demultiplexer_5_out13), .col14(demultiplexer_5_out14),
    .col15(demultiplexer_5_out15), .col16(demultiplexer_5_out16), .col17(demultiplexer_5_out17),
    .col18(demultiplexer_5_out18), .col19(demultiplexer_5_out19), .col20(demultiplexer_5_out20),
    .col21(demultiplexer_5_out21), .col22(demultiplexer_5_out22), .col23(demultiplexer_5_out23),
    .col24(demultiplexer_5_out24), .col25(demultiplexer_5_out25), .col26(demultiplexer_5_out26),
    .col27(demultiplexer_5_out27), .col28(demultiplexer_5_out28), .col29(demultiplexer_5_out29),
    .col30(demultiplexer_5_out30), .col31(demultiplexer_5_out31));
  DotMatrix #(.matrixcols(32), .matrixrows(32), .persist(30)) dotmatrix_4 (
    .col0(demultiplexer_6_out0), .col1(demultiplexer_6_out1), .col2(demultiplexer_6_out2),
    .col3(demultiplexer_6_out3), .col4(demultiplexer_6_out4), .col5(demultiplexer_6_out5),
    .col6(demultiplexer_6_out6), .col7(demultiplexer_6_out7), .col8(demultiplexer_6_out8),
    .col9(demultiplexer_6_out9), .col10(demultiplexer_6_out10), .col11(demultiplexer_6_out11),
    .col12(demultiplexer_6_out12), .col13(demultiplexer_6_out13), .col14(demultiplexer_6_out14),
    .col15(demultiplexer_6_out15), .col16(demultiplexer_6_out16), .col17(demultiplexer_6_out17),
    .col18(demultiplexer_6_out18), .col19(demultiplexer_6_out19), .col20(demultiplexer_6_out20),
    .col21(demultiplexer_6_out21), .col22(demultiplexer_6_out22), .col23(demultiplexer_6_out23),
    .col24(demultiplexer_6_out24), .col25(demultiplexer_6_out25), .col26(demultiplexer_6_out26),
    .col27(demultiplexer_6_out27), .col28(demultiplexer_6_out28), .col29(demultiplexer_6_out29),
    .col30(demultiplexer_6_out30), .col31(demultiplexer_6_out31));
  Demultiplexer #(.select(5), .width(32)) demultiplexer_5 (
    .out0(demultiplexer_5_out0), .out1(demultiplexer_5_out1), .out2(demultiplexer_5_out2),
    .out3(demultiplexer_5_out3), .out4(demultiplexer_5_out4), .out5(demultiplexer_5_out5),
    .out6(demultiplexer_5_out6), .out7(demultiplexer_5_out7), .out8(demultiplexer_5_out8),
    .out9(demultiplexer_5_out9), .out10(demultiplexer_5_out10), .out11(demultiplexer_5_out11),
    .out12(demultiplexer_5_out12), .out13(demultiplexer_5_out13), .out14(demultiplexer_5_out14),
    .out15(demultiplexer_5_out15), .out16(demultiplexer_5_out16), .out17(demultiplexer_5_out17),
    .out18(demultiplexer_5_out18), .out19(demultiplexer_5_out19), .out20(demultiplexer_5_out20),
    .out21(demultiplexer_5_out21), .out22(demultiplexer_5_out22), .out23(demultiplexer_5_out23),
    .out24(demultiplexer_5_out24), .out25(demultiplexer_5_out25), .out26(demultiplexer_5_out26),
    .out27(demultiplexer_5_out27), .out28(demultiplexer_5_out28), .out29(demultiplexer_5_out29),
    .out30(demultiplexer_5_out30), .out31(demultiplexer_5_out31), .in(TR_DATA), .sel(TR));  // open: en
  Demultiplexer #(.select(5), .width(32)) demultiplexer_6 (
    .out0(demultiplexer_6_out0), .out1(demultiplexer_6_out1), .out2(demultiplexer_6_out2),
    .out3(demultiplexer_6_out3), .out4(demultiplexer_6_out4), .out5(demultiplexer_6_out5),
    .out6(demultiplexer_6_out6), .out7(demultiplexer_6_out7), .out8(demultiplexer_6_out8),
    .out9(demultiplexer_6_out9), .out10(demultiplexer_6_out10), .out11(demultiplexer_6_out11),
    .out12(demultiplexer_6_out12), .out13(demultiplexer_6_out13), .out14(demultiplexer_6_out14),
    .out15(demultiplexer_6_out15), .out16(demultiplexer_6_out16), .out17(demultiplexer_6_out17),
    .out18(demultiplexer_6_out18), .out19(demultiplexer_6_out19), .out20(demultiplexer_6_out20),
    .out21(demultiplexer_6_out21), .out22(demultiplexer_6_out22), .out23(demultiplexer_6_out23),
    .out24(demultiplexer_6_out24), .out25(demultiplexer_6_out25), .out26(demultiplexer_6_out26),
    .out27(demultiplexer_6_out27), .out28(demultiplexer_6_out28), .out29(demultiplexer_6_out29),
    .out30(demultiplexer_6_out30), .out31(demultiplexer_6_out31), .in(BR_DATA), .sel(BR));  // open: en
  and and_1 (and_1_out, 1'b1, LEFT);
  or or_1 (or_1_out, LEFT, RIGHT);
  Keyboard #(.buflen(7)) keyboard_1 (.clk(CLK), .clr(undriven), .data(keyboard_1_data));  // open: re, avail
  KeyboardInputAWSD_main main_1 (
    .out_3(UP), .Down_pressed(DOWN), .Left_pressed(LEFT), .Right_pressed(RIGHT),
    .Keyboard_out(keyboard_1_data), .Keyboard_rst(undriven));
  Counter #(.width(6), .max('h3f)) counter_4 (
    .load(and_1_out), .Q(XPOS), .clk(or_1_out));  // open: D, count, carry, clr
  and and_2 (and_2_out, 1'b1, UP);
  or or_2 (or_2_out, UP, DOWN);
  Counter #(.width(6), .max('h3f)) counter_5 (
    .load(and_2_out), .Q(YPOS), .clk(or_2_out));  // open: D, count, carry, clr

  // Notes on the sheet:
  //   contents of rom_1 (hex, n*v repeats v):
  //   1b 11 0 11 1b
  //   FIELD SIZE X
  //   X POSITION
  //   FIELD SIZE Y
  //   Y POSITION
endmodule
