// Logisim project tick.circ as structural Verilog: 1 circuit, main circuit main
module main (
  input  in_1,
  input  in_2,
  output out_3
);

  wire d_ff_1_q, d_ff_1_qn, d_ff_2_q, not_1_out;

  not not_1 (not_1_out, in_1);
  D_Flip_Flop d_ff_1 (.clk(in_1), .D(in_2), .Q(d_ff_1_q), .Qn(d_ff_1_qn));  // open: preset, en, reset
  D_Flip_Flop d_ff_2 (.clk(not_1_out), .D(d_ff_1_qn), .Q(d_ff_2_q));  // open: Qn, preset, en, reset
  and and_1 (out_3, d_ff_1_q, d_ff_2_q);
endmodule
