// Logisim project timer.circ as structural Verilog: 1 circuit, main circuit main
module main (
  input  GAME_START,
  input  in_2
);

  wire _1_out, _2_out, _3_out, clock_1_out, counter_1_carry, main_1_out_2, main_2_out_2, NONE_out, not_1_out,
       not_2_out, not_3_out, not_4_out, not_5_out, not_6_out, not_7_out, not_8_out, pull_resistor_1_node,
       pull_resistor_2_node, pull_resistor_3_node, pull_resistor_4_node, T1, T2, T3, WRITE1, WRITE2, WRITE3;
  wire [31:0] buffer_1_out, buffer_2_out, buffer_3_out, buffer_4_out, buffer_5_out, buffer_6_out,
       buffer_7_out, buffer_8_out, buffer_9_out, CURRENT_TIME, DATA, DATA1, DATA2, DATA3, DATA_IN;

  Clock clock_1 (.out(clock_1_out));
  Counter #(.width(6), .max('h3f)) counter_1 (
    .carry(counter_1_carry), .clk(clock_1_out), .clr(not_1_out));  // open: load, D, count, Q
  not not_1 (not_1_out, GAME_START);
  Counter #(.width(32), .max('hffffffff)) counter_2 (
    .Q(CURRENT_TIME), .clk(counter_1_carry), .clr(not_1_out));  // open: load, D, count, carry
  assign buffer_1_out = DATA1;  // Buffer buffer_1, 32 bits wide
  assign buffer_2_out = DATA2;  // Buffer buffer_2, 32 bits wide
  assign buffer_3_out = DATA3;  // Buffer buffer_3, 32 bits wide
  Register #(.width(32)) register_1 (.D(CURRENT_TIME), .Q(DATA), .clk(not_1_out));  // open: en, clr
  assign buffer_4_out = buffer_1_out;  // Buffer buffer_4, 32 bits wide
  assign buffer_5_out = buffer_4_out;  // Buffer buffer_5, 32 bits wide
  assign buffer_6_out = buffer_2_out;  // Buffer buffer_6, 32 bits wide
  assign buffer_7_out = buffer_6_out;  // Buffer buffer_7, 32 bits wide
  assign buffer_8_out = buffer_9_out;  // Buffer buffer_8, 32 bits wide
  assign buffer_9_out = buffer_3_out;  // Buffer buffer_9, 32 bits wide
  // Probe on CURRENT_TIME
  // Probe on DATA
  Comparator #(.width(32), .mode("unsigned")) comparator_1 (.a(DATA), .b(buffer_5_out), .lt(T1));  // open: gt, eq
  Comparator #(.width(32), .mode("unsigned")) comparator_2 (.a(DATA), .b(buffer_7_out), .lt(T2));  // open: gt, eq
  Comparator #(.width(32), .mode("unsigned")) comparator_3 (.a(DATA), .b(buffer_8_out), .lt(T3));  // open: gt, eq
  assign DATA_IN = not_2_out ? DATA : 32'bz;  // Controlled_Buffer controlled_buffer_1
  not not_2 (not_2_out, in_2);
  assign DATA_IN = in_2 ? {32{1'b1}} : 32'bz;  // Controlled_Buffer controlled_buffer_2
  not not_3 (not_3_out, T1);
  not not_4 (not_4_out, T1);
  not not_5 (not_5_out, T2);
  not not_6 (not_6_out, T1);
  not not_7 (not_7_out, T2);
  not not_8 (not_8_out, T3);
  tick_main main_1 (.in_1(not_1_out), .out_2(main_1_out_2));
  and _1 (_1_out, T1, T2, T3);
  and _2 (_2_out, not_3_out, T2, T3);
  and _3 (_3_out, not_4_out, not_5_out, T3);
  and NONE (NONE_out, not_6_out, not_7_out, not_8_out);
  tick_main main_2 (.in_1(in_2), .out_2(main_2_out_2));
  Pull_Resistor pull_resistor_1 (.node(pull_resistor_1_node));
  assign pull_resistor_1_node = main_1_out_2 ? _1_out : 1'bz;  // Controlled_Buffer controlled_buffer_3
  Pull_Resistor pull_resistor_2 (.node(pull_resistor_2_node));
  assign pull_resistor_2_node = main_1_out_2 ? _2_out : 1'bz;  // Controlled_Buffer controlled_buffer_4
  Pull_Resistor pull_resistor_3 (.node(pull_resistor_3_node));
  assign pull_resistor_3_node = main_1_out_2 ? _3_out : 1'bz;  // Controlled_Buffer controlled_buffer_5
  Pull_Resistor pull_resistor_4 (.node(pull_resistor_4_node));
  assign pull_resistor_4_node = main_1_out_2 ? NONE_out : 1'bz;  // Controlled_Buffer controlled_buffer_6
  Register #(.width(32), .trigger("high")) register_2 (.D(DATA_IN), .Q(DATA1), .clk(WRITE1));  // open: en, clr
  Register #(.width(32), .trigger("high")) register_3 (.D(DATA_IN), .Q(DATA2), .clk(WRITE2));  // open: en, clr
  Register #(.width(32), .trigger("high")) register_4 (.D(DATA_IN), .Q(DATA3), .clk(WRITE3));  // open: en, clr
  // Probe on DATA1
  // Probe on DATA2
  // Probe on DATA3
  or or_1 (WRITE1, main_2_out_2, pull_resistor_1_node);
  or or_2 (WRITE2, main_2_out_2, pull_resistor_2_node);
  or or_3 (WRITE3, main_2_out_2, pull_resistor_3_node);

  // Other names for the same wires on the sheet: FIRST_RUN = in_2

  // Notes on the sheet:
  //   1
  //   2
  //   3
endmodule
